// Logisim project or.circ as structural Verilog: 13 circuits, main circuit or_gate
module or_gate (
  input  in_1,
  input  in_2,
  output out_3
);

  wire transistor_1_out, transistor_2_out;

  Transistor transistor_1 (.in(1'b1), .out(transistor_1_out), .gate(in_1));
  Transistor transistor_2 (.in(transistor_1_out), .out(transistor_2_out), .gate(in_2));
  Transistor #(.\type ("n")) transistor_3 (.in(1'b0), .out(transistor_2_out), .gate(in_1));
  Transistor #(.\type ("n")) transistor_4 (.in(1'b0), .out(transistor_2_out), .gate(in_2));
  Transistor transistor_5 (.in(1'b1), .out(out_3), .gate(transistor_2_out));
  Transistor #(.\type ("n")) transistor_6 (.in(1'b0), .out(out_3), .gate(transistor_2_out));

  // Notes on the sheet:
  //   或门
endmodule

module Xor_gate (
  input  in_1,
  input  nB,
  output out_3
);

  wire not_1_out, not_2_out, transistor_1_out, transistor_2_out, transistor_7_out, transistor_8_out;

  not not_1 (not_1_out, in_1);
  not not_2 (not_2_out, nB);
  Transistor transistor_1 (.in(1'b1), .out(transistor_1_out), .gate(in_1));
  Transistor transistor_2 (.in(1'b1), .out(transistor_2_out), .gate(not_1_out));
  Transistor transistor_3 (.in(transistor_1_out), .out(out_3), .gate(not_2_out));
  Transistor transistor_4 (.in(transistor_2_out), .out(out_3), .gate(nB));
  Transistor #(.\type ("n")) transistor_5 (.in(transistor_7_out), .out(out_3), .gate(nB));
  Transistor #(.\type ("n")) transistor_6 (.in(transistor_8_out), .out(out_3), .gate(not_2_out));
  Transistor #(.\type ("n")) transistor_7 (.in(1'b0), .out(transistor_7_out), .gate(in_1));
  Transistor #(.\type ("n")) transistor_8 (.in(1'b0), .out(transistor_8_out), .gate(not_1_out));

  // Notes on the sheet:
  //   最少晶体管方案
  //   A
  //   ~A
  //   B
endmodule

module XNOR_gate (
  input  in_1,
  input  in_2,
  output out_3
);

  wire and_1_out, and_2_out, not_1_out, not_2_out;

  not not_1 (not_1_out, in_1);
  not not_2 (not_2_out, in_2);
  and and_1 (and_1_out, in_1, in_2);
  and and_2 (and_2_out, not_1_out, not_2_out);
  or or_1 (out_3, and_1_out, and_2_out);
endmodule

module XNOR_gatequan (
  input  in_1,
  input  in_2,
  output out_3
);

  wire transistor_1_out;

  Transistor transistor_1 (.in(1'b1), .out(transistor_1_out), .gate(in_1));
  Transistor #(.\type ("n")) transistor_2 (.in(1'b0), .out(transistor_1_out), .gate(in_1));
  Transistor transistor_3 (.in(transistor_1_out), .out(out_3), .gate(in_2));
  Transistor #(.\type ("n")) transistor_4 (.in(in_1), .out(out_3), .gate(in_2));
  Transistor transistor_5 (.in(in_2), .out(out_3), .gate(transistor_1_out));
  Transistor #(.\type ("n")) transistor_6 (.in(in_2), .out(out_3), .gate(in_1));

  // Notes on the sheet:
  //   同或最少晶体管
endmodule

module decoder_circuit (
  input  a,
  input  b,
  output x,
  output y,
  output z,
  output u
);

  wire not_1_out, not_2_out;

  // Probe on not_1_out
  not not_1 (not_1_out, a);
  not not_2 (not_2_out, b);
  and and_1 (x, not_1_out, not_2_out);
  and and_2 (y, b, not_1_out);
  and and_3 (z, a, not_2_out);
  and and_4 (u, a, b);
endmodule

module decoder_3to8 (
  input  n,
  input  a,
  input  b,
  output out_4,
  output out_5,
  output out_6,
  output out_7,
  output out_8,
  output out_9,
  output out_10,
  output out_11
);

  wire decoder_circuit_1_u, decoder_circuit_1_x, decoder_circuit_1_y, decoder_circuit_1_z,
       decoder_circuit_2_u, decoder_circuit_2_x, decoder_circuit_2_y, decoder_circuit_2_z;

  and and_1 (out_4, decoder_circuit_1_x, ~n);  // AND_Gate
  and and_2 (out_5, decoder_circuit_1_y, ~n);  // AND_Gate
  decoder_circuit decoder_circuit_1 (
    .a(a), .b(b), .x(decoder_circuit_1_x), .y(decoder_circuit_1_y), .z(decoder_circuit_1_z),
    .u(decoder_circuit_1_u));
  and and_3 (out_6, decoder_circuit_1_z, ~n);  // AND_Gate
  and and_4 (out_8, n, decoder_circuit_2_x);
  decoder_circuit decoder_circuit_2 (
    .a(a), .b(b), .x(decoder_circuit_2_x), .y(decoder_circuit_2_y), .z(decoder_circuit_2_z),
    .u(decoder_circuit_2_u));
  and and_5 (out_9, n, decoder_circuit_2_y);
  and and_6 (out_10, decoder_circuit_2_z, n);
  and and_7 (out_11, decoder_circuit_2_u, n);
  and and_8 (out_7, decoder_circuit_1_u, ~n);  // AND_Gate
endmodule

module seven_code_trans (
  input  in_1,
  input  in_2,
  input  in_3,
  input  in_4
);

  wire decoder_1_out0, decoder_1_out1, decoder_1_out2, decoder_1_out3, decoder_1_out4, decoder_1_out5,
       decoder_1_out6, decoder_1_out7, decoder_1_out8, decoder_1_out9, decoder_1_out10, decoder_1_out11,
       decoder_1_out12, decoder_1_out13, decoder_1_out14, decoder_1_out15, or_1_out, or_2_out, or_3_out,
       or_4_out, or_5_out, or_6_out, or_7_out, or_8_out;

  Decoder #(.select(4)) decoder_1 (
    .out0(decoder_1_out0), .out1(decoder_1_out1), .out2(decoder_1_out2), .out3(decoder_1_out3),
    .out4(decoder_1_out4), .out5(decoder_1_out5), .out6(decoder_1_out6), .out7(decoder_1_out7),
    .out8(decoder_1_out8), .out9(decoder_1_out9), .out10(decoder_1_out10), .out11(decoder_1_out11),
    .out12(decoder_1_out12), .out13(decoder_1_out13), .out14(decoder_1_out14), .out15(decoder_1_out15),
    .sel({in_4, in_3, in_2, in_1}), .en(1'b1));
  or or_1 (or_1_out, decoder_1_out2, decoder_1_out3, decoder_1_out4, decoder_1_out5, decoder_1_out6, decoder_1_out8, decoder_1_out9);
  _7_Segment_Display u_7_segment_display_1 (
    .g(or_1_out), .f(or_2_out), .a(or_3_out), .b(or_4_out), .e(or_5_out), .d(or_6_out), .c(or_7_out),
    .dp(or_8_out));
  or or_2 (or_2_out, decoder_1_out0, decoder_1_out4, decoder_1_out5, decoder_1_out6, decoder_1_out8, decoder_1_out9);
  or or_3 (or_3_out, decoder_1_out0, decoder_1_out2, decoder_1_out3, decoder_1_out5, decoder_1_out6, decoder_1_out7, decoder_1_out8, decoder_1_out9);
  or or_4 (or_4_out, decoder_1_out0, decoder_1_out1, decoder_1_out2, decoder_1_out3, decoder_1_out7, decoder_1_out8, decoder_1_out9, decoder_1_out4);
  or or_5 (or_5_out, decoder_1_out0, decoder_1_out2, decoder_1_out6, decoder_1_out8);
  or or_6 (or_6_out, decoder_1_out0, decoder_1_out3, decoder_1_out9, decoder_1_out2, decoder_1_out5, decoder_1_out6, decoder_1_out8);
  or or_7 (or_7_out, decoder_1_out0, decoder_1_out1, decoder_1_out4, decoder_1_out3, decoder_1_out5, decoder_1_out6, decoder_1_out7, decoder_1_out8, decoder_1_out9);
  or or_8 (or_8_out, decoder_1_out13, decoder_1_out12, decoder_1_out11, decoder_1_out10, decoder_1_out14, decoder_1_out15);

  // Notes on the sheet:
  //   1
  //   8
  //   1
  //   2
  //   3
  //   4
  //   5
  //   6
  //   7
endmodule

module seven_code_16_trans (
  input  m0,
  input  m1,
  input  m2,
  input  m3,
  output a,
  output b,
  output c,
  output d,
  output e,
  output f,
  output g
);

  wire decoder_1_out0, decoder_1_out1, decoder_1_out2, decoder_1_out3, decoder_1_out4, decoder_1_out5,
       decoder_1_out6, decoder_1_out7, decoder_1_out8, decoder_1_out9, decoder_1_out10, decoder_1_out11,
       decoder_1_out12, decoder_1_out13, decoder_1_out14, decoder_1_out15;

  Decoder #(.select(4)) decoder_1 (
    .out0(decoder_1_out0), .out1(decoder_1_out1), .out2(decoder_1_out2), .out3(decoder_1_out3),
    .out4(decoder_1_out4), .out5(decoder_1_out5), .out6(decoder_1_out6), .out7(decoder_1_out7),
    .out8(decoder_1_out8), .out9(decoder_1_out9), .out10(decoder_1_out10), .out11(decoder_1_out11),
    .out12(decoder_1_out12), .out13(decoder_1_out13), .out14(decoder_1_out14), .out15(decoder_1_out15),
    .sel({m3, m2, m1, m0}), .en(1'b1));
  or or_1 (d, decoder_1_out10, decoder_1_out0, decoder_1_out1, decoder_1_out2, decoder_1_out3, decoder_1_out7, decoder_1_out8, decoder_1_out9, decoder_1_out4, decoder_1_out13);
  or or_2 (a, decoder_1_out10, decoder_1_out11, decoder_1_out5, decoder_1_out2, decoder_1_out3, decoder_1_out4, decoder_1_out6, decoder_1_out8, decoder_1_out9, decoder_1_out13, decoder_1_out14, decoder_1_out15);
  _7_Segment_Display u_7_segment_display_1 (.g(a), .f(b), .a(c), .b(d), .e(e), .d(f), .c(g));  // open: dp
  or or_3 (g, decoder_1_out10, decoder_1_out5, decoder_1_out0, decoder_1_out1, decoder_1_out4, decoder_1_out3, decoder_1_out6, decoder_1_out7, decoder_1_out8, decoder_1_out9, decoder_1_out11, decoder_1_out13);
  or or_4 (f, decoder_1_out14, decoder_1_out13, decoder_1_out0, decoder_1_out3, decoder_1_out9, decoder_1_out2, decoder_1_out5, decoder_1_out6, decoder_1_out8, decoder_1_out12, decoder_1_out11);
  or or_5 (b, decoder_1_out10, decoder_1_out11, decoder_1_out0, decoder_1_out4, decoder_1_out5, decoder_1_out12, decoder_1_out6, decoder_1_out8, decoder_1_out9, decoder_1_out15, decoder_1_out14);
  or or_6 (c, decoder_1_out14, decoder_1_out15, decoder_1_out0, decoder_1_out2, decoder_1_out3, decoder_1_out5, decoder_1_out6, decoder_1_out7, decoder_1_out8, decoder_1_out10, decoder_1_out12, decoder_1_out9);
  or or_7 (e, decoder_1_out15, decoder_1_out14, decoder_1_out13, decoder_1_out0, decoder_1_out2, decoder_1_out6, decoder_1_out8, decoder_1_out12, decoder_1_out11, decoder_1_out10);

  // Notes on the sheet:
  //   1
  //   1
  //   2
  //   3
  //   4
  //   5
  //   6
  //   7
endmodule

module encoder (
);

  wire dipswitch_1_sw2, dipswitch_1_sw3, dipswitch_1_sw4, dipswitch_1_sw5, dipswitch_1_sw6, dipswitch_1_sw7,
       dipswitch_1_sw8, dipswitch_1_sw9, dipswitch_1_sw10, dipswitch_1_sw11, dipswitch_1_sw12,
       dipswitch_1_sw13, dipswitch_1_sw14, dipswitch_1_sw15, dipswitch_1_sw16, or_1_out, or_2_out, or_3_out,
       or_4_out, seven_code_16_trans_1_a, seven_code_16_trans_1_b, seven_code_16_trans_1_c,
       seven_code_16_trans_1_d, seven_code_16_trans_1_e, seven_code_16_trans_1_f, seven_code_16_trans_1_g;

  DipSwitch #(.number(16)) dipswitch_1 (
    .sw2(dipswitch_1_sw2), .sw3(dipswitch_1_sw3), .sw4(dipswitch_1_sw4), .sw5(dipswitch_1_sw5),
    .sw6(dipswitch_1_sw6), .sw7(dipswitch_1_sw7), .sw8(dipswitch_1_sw8), .sw9(dipswitch_1_sw9),
    .sw10(dipswitch_1_sw10), .sw11(dipswitch_1_sw11), .sw12(dipswitch_1_sw12), .sw13(dipswitch_1_sw13),
    .sw14(dipswitch_1_sw14), .sw15(dipswitch_1_sw15), .sw16(dipswitch_1_sw16));  // open: sw1
  or or_1 (or_1_out, dipswitch_1_sw2, dipswitch_1_sw4, dipswitch_1_sw6, dipswitch_1_sw8, dipswitch_1_sw10, dipswitch_1_sw12, dipswitch_1_sw14, dipswitch_1_sw16);
  or or_2 (or_2_out, dipswitch_1_sw3, dipswitch_1_sw4, dipswitch_1_sw7, dipswitch_1_sw8, dipswitch_1_sw11, dipswitch_1_sw12, dipswitch_1_sw15, dipswitch_1_sw16);
  or or_3 (or_3_out, dipswitch_1_sw5, dipswitch_1_sw6, dipswitch_1_sw7, dipswitch_1_sw8, dipswitch_1_sw13, dipswitch_1_sw14, dipswitch_1_sw15, dipswitch_1_sw16);
  or or_4 (or_4_out, dipswitch_1_sw9, dipswitch_1_sw10, dipswitch_1_sw11, dipswitch_1_sw12, dipswitch_1_sw13, dipswitch_1_sw14, dipswitch_1_sw15, dipswitch_1_sw16);
  seven_code_16_trans seven_code_16_trans_1 (
    .m0(or_1_out), .m1(or_2_out), .m2(or_3_out), .m3(or_4_out), .a(seven_code_16_trans_1_a),
    .b(seven_code_16_trans_1_b), .c(seven_code_16_trans_1_c), .d(seven_code_16_trans_1_d),
    .e(seven_code_16_trans_1_e), .f(seven_code_16_trans_1_f), .g(seven_code_16_trans_1_g));
  _7_Segment_Display u_7_segment_display_1 (
    .g(seven_code_16_trans_1_a), .f(seven_code_16_trans_1_b), .a(seven_code_16_trans_1_c),
    .b(seven_code_16_trans_1_d), .e(seven_code_16_trans_1_e), .d(seven_code_16_trans_1_f),
    .c(seven_code_16_trans_1_g));  // open: dp

  // Notes on the sheet:
  //   0
  //   15
endmodule

module encoder_privil (
  input  A0,
  input  A1,
  input  A2,
  input  A3,
  output Y0,
  output Y1
);

  wire and_1_out, and_2_out, seven_code_16_trans_1_a, seven_code_16_trans_1_b, seven_code_16_trans_1_c,
       seven_code_16_trans_1_d, seven_code_16_trans_1_e, seven_code_16_trans_1_f, seven_code_16_trans_1_g;

  or or_1 (Y0, A3, and_1_out);
  and and_1 (and_1_out, A1, ~A2, ~A3);  // AND_Gate
  or or_2 (Y1, A3, and_2_out);
  and and_2 (and_2_out, ~A3, A2);  // AND_Gate
  seven_code_16_trans seven_code_16_trans_1 (
    .m0(Y0), .m1(Y1), .m2(1'b0), .m3(1'b0), .a(seven_code_16_trans_1_a), .b(seven_code_16_trans_1_b),
    .c(seven_code_16_trans_1_c), .d(seven_code_16_trans_1_d), .e(seven_code_16_trans_1_e),
    .f(seven_code_16_trans_1_f), .g(seven_code_16_trans_1_g));
  _7_Segment_Display u_7_segment_display_1 (
    .g(seven_code_16_trans_1_a), .f(seven_code_16_trans_1_b), .a(seven_code_16_trans_1_c),
    .b(seven_code_16_trans_1_d), .e(seven_code_16_trans_1_e), .d(seven_code_16_trans_1_f),
    .c(seven_code_16_trans_1_g));  // open: dp
endmodule

module encoder_16to4 (
);

  wire dipswitch_1_sw1, dipswitch_1_sw2, dipswitch_1_sw3, dipswitch_1_sw4, dipswitch_1_sw5, dipswitch_1_sw6,
       dipswitch_1_sw7, dipswitch_1_sw8, dipswitch_1_sw9, dipswitch_1_sw10, dipswitch_1_sw11,
       dipswitch_1_sw12, dipswitch_1_sw13, dipswitch_1_sw14, dipswitch_1_sw15, dipswitch_1_sw16,
       encoder_privil_1_y0, encoder_privil_1_y1, encoder_privil_2_y0, encoder_privil_2_y1,
       encoder_privil_3_y0, encoder_privil_3_y1, encoder_privil_4_y0, encoder_privil_4_y1,
       encoder_privil_5_y0, encoder_privil_5_y1, encoder_privil_6_y0, encoder_privil_6_y1,
       encoder_privil_7_y0, encoder_privil_7_y1, encoder_privil_8_y0, encoder_privil_8_y1, or_1_out,
       or_2_out, or_3_out, or_4_out, seven_code_16_trans_1_a, seven_code_16_trans_1_b,
       seven_code_16_trans_1_c, seven_code_16_trans_1_d, seven_code_16_trans_1_e, seven_code_16_trans_1_f,
       seven_code_16_trans_1_g;

  DipSwitch #(.number(16)) dipswitch_1 (
    .sw1(dipswitch_1_sw1), .sw2(dipswitch_1_sw2), .sw3(dipswitch_1_sw3), .sw4(dipswitch_1_sw4),
    .sw5(dipswitch_1_sw5), .sw6(dipswitch_1_sw6), .sw7(dipswitch_1_sw7), .sw8(dipswitch_1_sw8),
    .sw9(dipswitch_1_sw9), .sw10(dipswitch_1_sw10), .sw11(dipswitch_1_sw11), .sw12(dipswitch_1_sw12),
    .sw13(dipswitch_1_sw13), .sw14(dipswitch_1_sw14), .sw15(dipswitch_1_sw15), .sw16(dipswitch_1_sw16));
  or or_1 (or_1_out, dipswitch_1_sw1, dipswitch_1_sw2, dipswitch_1_sw3, dipswitch_1_sw4);
  or or_2 (or_2_out, dipswitch_1_sw5, dipswitch_1_sw6, dipswitch_1_sw7, dipswitch_1_sw8);
  or or_3 (or_3_out, dipswitch_1_sw9, dipswitch_1_sw10, dipswitch_1_sw11, dipswitch_1_sw12);
  or or_4 (or_4_out, dipswitch_1_sw13, dipswitch_1_sw14, dipswitch_1_sw15, dipswitch_1_sw16);
  encoder_privil encoder_privil_1 (
    .A0(dipswitch_1_sw1), .A1(dipswitch_1_sw2), .A2(dipswitch_1_sw3), .A3(dipswitch_1_sw4),
    .Y0(encoder_privil_1_y0), .Y1(encoder_privil_1_y1));
  encoder_privil encoder_privil_2 (
    .A0(dipswitch_1_sw5), .A1(dipswitch_1_sw6), .A2(dipswitch_1_sw7), .A3(dipswitch_1_sw8),
    .Y0(encoder_privil_2_y0), .Y1(encoder_privil_2_y1));
  encoder_privil encoder_privil_3 (
    .A0(or_1_out), .A1(or_2_out), .A2(or_3_out), .A3(or_4_out), .Y0(encoder_privil_3_y0),
    .Y1(encoder_privil_3_y1));
  encoder_privil encoder_privil_4 (
    .A0(encoder_privil_1_y0), .A1(encoder_privil_1_y1), .A2(encoder_privil_2_y0), .A3(encoder_privil_2_y1),
    .Y0(encoder_privil_4_y0), .Y1(encoder_privil_4_y1));
  encoder_privil encoder_privil_5 (
    .A0(dipswitch_1_sw9), .A1(dipswitch_1_sw10), .A2(dipswitch_1_sw11), .A3(dipswitch_1_sw12),
    .Y0(encoder_privil_5_y0), .Y1(encoder_privil_5_y1));
  encoder_privil encoder_privil_6 (
    .A0(encoder_privil_4_y0), .A1(encoder_privil_4_y1), .A2(encoder_privil_5_y0), .A3(encoder_privil_5_y1),
    .Y0(encoder_privil_6_y0), .Y1(encoder_privil_6_y1));
  encoder_privil encoder_privil_7 (
    .A0(dipswitch_1_sw13), .A1(dipswitch_1_sw14), .A2(dipswitch_1_sw15), .A3(dipswitch_1_sw16),
    .Y0(encoder_privil_7_y0), .Y1(encoder_privil_7_y1));
  encoder_privil encoder_privil_8 (
    .A0(encoder_privil_6_y0), .A1(encoder_privil_6_y1), .A2(encoder_privil_7_y0), .A3(encoder_privil_7_y1),
    .Y0(encoder_privil_8_y0), .Y1(encoder_privil_8_y1));
  seven_code_16_trans seven_code_16_trans_1 (
    .m0(encoder_privil_8_y0), .m1(encoder_privil_8_y1), .m2(encoder_privil_3_y0), .m3(encoder_privil_3_y1),
    .a(seven_code_16_trans_1_a), .b(seven_code_16_trans_1_b), .c(seven_code_16_trans_1_c),
    .d(seven_code_16_trans_1_d), .e(seven_code_16_trans_1_e), .f(seven_code_16_trans_1_f),
    .g(seven_code_16_trans_1_g));
  _7_Segment_Display u_7_segment_display_1 (
    .g(seven_code_16_trans_1_a), .f(seven_code_16_trans_1_b), .a(seven_code_16_trans_1_c),
    .b(seven_code_16_trans_1_d), .e(seven_code_16_trans_1_e), .d(seven_code_16_trans_1_f),
    .c(seven_code_16_trans_1_g));  // open: dp
endmodule

module encoder_16to4_true (
);

  wire and_1_out, and_2_out, and_3_out, and_4_out, and_5_out, and_6_out, dipswitch_1_sw1, dipswitch_1_sw2,
       dipswitch_1_sw3, dipswitch_1_sw4, dipswitch_1_sw5, dipswitch_1_sw6, dipswitch_1_sw7, dipswitch_1_sw8,
       dipswitch_1_sw9, dipswitch_1_sw10, dipswitch_1_sw11, dipswitch_1_sw12, dipswitch_1_sw13,
       dipswitch_1_sw14, dipswitch_1_sw15, dipswitch_1_sw16, encoder_privil_1_y0, encoder_privil_1_y1,
       encoder_privil_2_y0, encoder_privil_2_y1, encoder_privil_3_y0, encoder_privil_3_y1,
       encoder_privil_4_y0, encoder_privil_4_y1, encoder_privil_5_y0, encoder_privil_5_y1, or_1_out,
       or_2_out, or_3_out, or_4_out, or_5_out, or_6_out, seven_code_16_trans_1_a, seven_code_16_trans_1_b,
       seven_code_16_trans_1_c, seven_code_16_trans_1_d, seven_code_16_trans_1_e, seven_code_16_trans_1_f,
       seven_code_16_trans_1_g;

  DipSwitch #(.number(16)) dipswitch_1 (
    .sw1(dipswitch_1_sw1), .sw2(dipswitch_1_sw2), .sw3(dipswitch_1_sw3), .sw4(dipswitch_1_sw4),
    .sw5(dipswitch_1_sw5), .sw6(dipswitch_1_sw6), .sw7(dipswitch_1_sw7), .sw8(dipswitch_1_sw8),
    .sw9(dipswitch_1_sw9), .sw10(dipswitch_1_sw10), .sw11(dipswitch_1_sw11), .sw12(dipswitch_1_sw12),
    .sw13(dipswitch_1_sw13), .sw14(dipswitch_1_sw14), .sw15(dipswitch_1_sw15), .sw16(dipswitch_1_sw16));
  or or_1 (or_1_out, dipswitch_1_sw1, dipswitch_1_sw2, dipswitch_1_sw3, dipswitch_1_sw4);
  or or_2 (or_2_out, dipswitch_1_sw5, dipswitch_1_sw6, dipswitch_1_sw7, dipswitch_1_sw8);
  or or_3 (or_3_out, dipswitch_1_sw9, dipswitch_1_sw10, dipswitch_1_sw11, dipswitch_1_sw12);
  or or_4 (or_4_out, dipswitch_1_sw13, dipswitch_1_sw14, dipswitch_1_sw15, dipswitch_1_sw16);
  encoder_privil encoder_privil_1 (
    .A0(dipswitch_1_sw1), .A1(dipswitch_1_sw2), .A2(dipswitch_1_sw3), .A3(dipswitch_1_sw4),
    .Y0(encoder_privil_1_y0), .Y1(encoder_privil_1_y1));
  encoder_privil encoder_privil_2 (
    .A0(dipswitch_1_sw5), .A1(dipswitch_1_sw6), .A2(dipswitch_1_sw7), .A3(dipswitch_1_sw8),
    .Y0(encoder_privil_2_y0), .Y1(encoder_privil_2_y1));
  encoder_privil encoder_privil_3 (
    .A0(dipswitch_1_sw9), .A1(dipswitch_1_sw10), .A2(dipswitch_1_sw11), .A3(dipswitch_1_sw12),
    .Y0(encoder_privil_3_y0), .Y1(encoder_privil_3_y1));
  encoder_privil encoder_privil_4 (
    .A0(dipswitch_1_sw13), .A1(dipswitch_1_sw14), .A2(dipswitch_1_sw15), .A3(dipswitch_1_sw16),
    .Y0(encoder_privil_4_y0), .Y1(encoder_privil_4_y1));
  encoder_privil encoder_privil_5 (
    .A0(or_1_out), .A1(or_2_out), .A2(or_3_out), .A3(or_4_out), .Y0(encoder_privil_5_y0),
    .Y1(encoder_privil_5_y1));
  and and_1 (and_1_out, encoder_privil_1_y0, ~encoder_privil_2_y0, ~encoder_privil_2_y1, ~encoder_privil_3_y0, ~encoder_privil_3_y1, ~encoder_privil_4_y0, ~encoder_privil_4_y1);  // AND_Gate
  and and_2 (and_2_out, encoder_privil_1_y1, ~encoder_privil_2_y0, ~encoder_privil_2_y1, ~encoder_privil_3_y0, ~encoder_privil_3_y1, ~encoder_privil_4_y0, ~encoder_privil_4_y1);  // AND_Gate
  and and_3 (and_3_out, encoder_privil_2_y0, ~encoder_privil_3_y0, ~encoder_privil_3_y1, ~encoder_privil_4_y0, ~encoder_privil_4_y1);  // AND_Gate
  and and_4 (and_4_out, encoder_privil_2_y1, ~encoder_privil_3_y0, ~encoder_privil_3_y1, ~encoder_privil_4_y0, ~encoder_privil_4_y1);  // AND_Gate
  and and_5 (and_5_out, encoder_privil_3_y0, ~encoder_privil_4_y0, ~encoder_privil_4_y1);  // AND_Gate
  and and_6 (and_6_out, encoder_privil_3_y1, ~encoder_privil_4_y0, ~encoder_privil_4_y1);  // AND_Gate
  or or_5 (or_5_out, and_1_out, and_3_out, and_5_out, encoder_privil_4_y0);
  or or_6 (or_6_out, and_2_out, and_4_out, and_6_out, encoder_privil_4_y1);
  _7_Segment_Display u_7_segment_display_1 (
    .g(seven_code_16_trans_1_a), .f(seven_code_16_trans_1_b), .a(seven_code_16_trans_1_c),
    .b(seven_code_16_trans_1_d), .e(seven_code_16_trans_1_e), .d(seven_code_16_trans_1_f),
    .c(seven_code_16_trans_1_g));  // open: dp
  seven_code_16_trans seven_code_16_trans_1 (
    .m0(or_5_out), .m1(or_6_out), .m2(encoder_privil_5_y0), .m3(encoder_privil_5_y1),
    .a(seven_code_16_trans_1_a), .b(seven_code_16_trans_1_b), .c(seven_code_16_trans_1_c),
    .d(seven_code_16_trans_1_d), .e(seven_code_16_trans_1_e), .f(seven_code_16_trans_1_f),
    .g(seven_code_16_trans_1_g));
endmodule

module encoder_16to4_true1 (
);

  wire and_1_out, and_2_out, and_3_out, and_4_out, and_5_out, and_6_out, and_7_out, and_8_out,
       dipswitch_1_sw1, dipswitch_1_sw2, dipswitch_1_sw3, dipswitch_1_sw4, dipswitch_1_sw5, dipswitch_1_sw6,
       dipswitch_1_sw7, dipswitch_1_sw8, dipswitch_1_sw9, dipswitch_1_sw10, dipswitch_1_sw11,
       dipswitch_1_sw12, dipswitch_1_sw13, dipswitch_1_sw14, dipswitch_1_sw15, dipswitch_1_sw16,
       encoder_privil_1_y0, encoder_privil_1_y1, encoder_privil_2_y0, encoder_privil_2_y1,
       encoder_privil_3_y0, encoder_privil_3_y1, encoder_privil_4_y0, encoder_privil_4_y1,
       encoder_privil_5_y0, encoder_privil_5_y1, or_1_out, or_2_out, or_3_out, or_4_out, or_5_out, or_6_out,
       seven_code_16_trans_1_a, seven_code_16_trans_1_b, seven_code_16_trans_1_c, seven_code_16_trans_1_d,
       seven_code_16_trans_1_e, seven_code_16_trans_1_f, seven_code_16_trans_1_g;

  DipSwitch #(.number(16)) dipswitch_1 (
    .sw1(dipswitch_1_sw1), .sw2(dipswitch_1_sw2), .sw3(dipswitch_1_sw3), .sw4(dipswitch_1_sw4),
    .sw5(dipswitch_1_sw5), .sw6(dipswitch_1_sw6), .sw7(dipswitch_1_sw7), .sw8(dipswitch_1_sw8),
    .sw9(dipswitch_1_sw9), .sw10(dipswitch_1_sw10), .sw11(dipswitch_1_sw11), .sw12(dipswitch_1_sw12),
    .sw13(dipswitch_1_sw13), .sw14(dipswitch_1_sw14), .sw15(dipswitch_1_sw15), .sw16(dipswitch_1_sw16));
  or or_1 (or_1_out, dipswitch_1_sw1, dipswitch_1_sw2, dipswitch_1_sw3, dipswitch_1_sw4);
  or or_2 (or_2_out, dipswitch_1_sw5, dipswitch_1_sw6, dipswitch_1_sw7, dipswitch_1_sw8);
  or or_3 (or_3_out, dipswitch_1_sw9, dipswitch_1_sw10, dipswitch_1_sw11, dipswitch_1_sw12);
  or or_4 (or_4_out, dipswitch_1_sw13, dipswitch_1_sw14, dipswitch_1_sw15, dipswitch_1_sw16);
  encoder_privil encoder_privil_1 (
    .A0(dipswitch_1_sw1), .A1(dipswitch_1_sw2), .A2(dipswitch_1_sw3), .A3(dipswitch_1_sw4),
    .Y0(encoder_privil_1_y0), .Y1(encoder_privil_1_y1));
  encoder_privil encoder_privil_2 (
    .A0(dipswitch_1_sw5), .A1(dipswitch_1_sw6), .A2(dipswitch_1_sw7), .A3(dipswitch_1_sw8),
    .Y0(encoder_privil_2_y0), .Y1(encoder_privil_2_y1));
  encoder_privil encoder_privil_3 (
    .A0(dipswitch_1_sw9), .A1(dipswitch_1_sw10), .A2(dipswitch_1_sw11), .A3(dipswitch_1_sw12),
    .Y0(encoder_privil_3_y0), .Y1(encoder_privil_3_y1));
  encoder_privil encoder_privil_4 (
    .A0(dipswitch_1_sw13), .A1(dipswitch_1_sw14), .A2(dipswitch_1_sw15), .A3(dipswitch_1_sw16),
    .Y0(encoder_privil_4_y0), .Y1(encoder_privil_4_y1));
  and and_1 (and_1_out, encoder_privil_1_y0, or_1_out, ~or_2_out, ~or_3_out, ~or_4_out);  // AND_Gate
  encoder_privil encoder_privil_5 (
    .A0(or_1_out), .A1(or_2_out), .A2(or_3_out), .A3(or_4_out), .Y0(encoder_privil_5_y0),
    .Y1(encoder_privil_5_y1));
  and and_2 (and_2_out, encoder_privil_1_y1, or_1_out, ~or_2_out, ~or_3_out, ~or_4_out);  // AND_Gate
  and and_3 (and_3_out, encoder_privil_2_y0, or_2_out, ~or_3_out, ~or_4_out);  // AND_Gate
  and and_4 (and_4_out, encoder_privil_2_y1, or_2_out, ~or_3_out, ~or_4_out);  // AND_Gate
  and and_5 (and_5_out, encoder_privil_3_y0, or_3_out, ~or_4_out);  // AND_Gate
  and and_6 (and_6_out, encoder_privil_3_y1, or_3_out, ~or_4_out);  // AND_Gate
  or or_5 (or_5_out, and_1_out, and_3_out, and_5_out, and_7_out);
  and and_7 (and_7_out, encoder_privil_4_y0, or_4_out);
  and and_8 (and_8_out, encoder_privil_4_y1, or_4_out);
  or or_6 (or_6_out, and_2_out, and_4_out, and_6_out, and_8_out);
  _7_Segment_Display u_7_segment_display_1 (
    .g(seven_code_16_trans_1_a), .f(seven_code_16_trans_1_b), .a(seven_code_16_trans_1_c),
    .b(seven_code_16_trans_1_d), .e(seven_code_16_trans_1_e), .d(seven_code_16_trans_1_f),
    .c(seven_code_16_trans_1_g));  // open: dp
  seven_code_16_trans seven_code_16_trans_1 (
    .m0(or_5_out), .m1(or_6_out), .m2(encoder_privil_5_y0), .m3(encoder_privil_5_y1),
    .a(seven_code_16_trans_1_a), .b(seven_code_16_trans_1_b), .c(seven_code_16_trans_1_c),
    .d(seven_code_16_trans_1_d), .e(seven_code_16_trans_1_e), .f(seven_code_16_trans_1_f),
    .g(seven_code_16_trans_1_g));
endmodule
