// Logisim project or_gemini.circ as structural Verilog: 52 circuits, main circuit or_gate
module or_gate (
  input  in_1,
  input  in_2,
  output out_3
);

  wire transistor_1_out, transistor_2_out;

  Transistor transistor_1 (.in(1'b1), .out(transistor_1_out), .gate(in_1));
  Transistor transistor_2 (.in(transistor_1_out), .out(transistor_2_out), .gate(in_2));
  Transistor #(.\type ("n")) transistor_3 (.in(1'b0), .out(transistor_2_out), .gate(in_1));
  Transistor #(.\type ("n")) transistor_4 (.in(1'b0), .out(transistor_2_out), .gate(in_2));
  Transistor transistor_5 (.in(1'b1), .out(out_3), .gate(transistor_2_out));
  Transistor #(.\type ("n")) transistor_6 (.in(1'b0), .out(out_3), .gate(transistor_2_out));

  // Notes on the sheet:
  //   或门
endmodule

module Xor_gate (
  input  in_1,
  input  nB,
  output out_3
);

  wire not_1_out, not_2_out, transistor_1_out, transistor_2_out, transistor_7_out, transistor_8_out;

  not not_1 (not_1_out, in_1);
  not not_2 (not_2_out, nB);
  Transistor transistor_1 (.in(1'b1), .out(transistor_1_out), .gate(in_1));
  Transistor transistor_2 (.in(1'b1), .out(transistor_2_out), .gate(not_1_out));
  Transistor transistor_3 (.in(transistor_1_out), .out(out_3), .gate(not_2_out));
  Transistor transistor_4 (.in(transistor_2_out), .out(out_3), .gate(nB));
  Transistor #(.\type ("n")) transistor_5 (.in(transistor_7_out), .out(out_3), .gate(nB));
  Transistor #(.\type ("n")) transistor_6 (.in(transistor_8_out), .out(out_3), .gate(not_2_out));
  Transistor #(.\type ("n")) transistor_7 (.in(1'b0), .out(transistor_7_out), .gate(in_1));
  Transistor #(.\type ("n")) transistor_8 (.in(1'b0), .out(transistor_8_out), .gate(not_1_out));

  // Notes on the sheet:
  //   最少晶体管方案
  //   A
  //   ~A
  //   B
endmodule

module XNOR_gate (
  input  in_1,
  input  in_2,
  output out_3
);

  wire and_1_out, and_2_out, not_1_out, not_2_out;

  not not_1 (not_1_out, in_1);
  not not_2 (not_2_out, in_2);
  and and_1 (and_1_out, in_1, in_2);
  and and_2 (and_2_out, not_1_out, not_2_out);
  or or_1 (out_3, and_1_out, and_2_out);
endmodule

module XNOR_gatequan (
  input  in_1,
  input  in_2,
  output out_3
);

  wire transistor_1_out;

  Transistor transistor_1 (.in(1'b1), .out(transistor_1_out), .gate(in_1));
  Transistor #(.\type ("n")) transistor_2 (.in(1'b0), .out(transistor_1_out), .gate(in_1));
  Transistor transistor_3 (.in(transistor_1_out), .out(out_3), .gate(in_2));
  Transistor #(.\type ("n")) transistor_4 (.in(in_1), .out(out_3), .gate(in_2));
  Transistor transistor_5 (.in(in_2), .out(out_3), .gate(transistor_1_out));
  Transistor #(.\type ("n")) transistor_6 (.in(in_2), .out(out_3), .gate(in_1));

  // Notes on the sheet:
  //   同或最少晶体管
endmodule

module decoder_circuit (
  input  a,
  input  b,
  output x,
  output y,
  output z,
  output u
);

  wire not_1_out, not_2_out;

  // Probe on not_1_out
  not not_1 (not_1_out, a);
  not not_2 (not_2_out, b);
  and and_1 (x, not_1_out, not_2_out);
  and and_2 (y, b, not_1_out);
  and and_3 (z, a, not_2_out);
  and and_4 (u, a, b);
endmodule

module decoder_3to8 (
  input  n,
  input  a,
  input  b,
  output out_4,
  output out_5,
  output out_6,
  output out_7,
  output out_8,
  output out_9,
  output out_10,
  output out_11
);

  wire decoder_circuit_1_u, decoder_circuit_1_x, decoder_circuit_1_y, decoder_circuit_1_z,
       decoder_circuit_2_u, decoder_circuit_2_x, decoder_circuit_2_y, decoder_circuit_2_z;

  and and_1 (out_4, decoder_circuit_1_x, ~n);  // AND_Gate
  and and_2 (out_5, decoder_circuit_1_y, ~n);  // AND_Gate
  decoder_circuit decoder_circuit_1 (
    .a(a), .b(b), .x(decoder_circuit_1_x), .y(decoder_circuit_1_y), .z(decoder_circuit_1_z),
    .u(decoder_circuit_1_u));
  and and_3 (out_6, decoder_circuit_1_z, ~n);  // AND_Gate
  and and_4 (out_8, n, decoder_circuit_2_x);
  decoder_circuit decoder_circuit_2 (
    .a(a), .b(b), .x(decoder_circuit_2_x), .y(decoder_circuit_2_y), .z(decoder_circuit_2_z),
    .u(decoder_circuit_2_u));
  and and_5 (out_9, n, decoder_circuit_2_y);
  and and_6 (out_10, decoder_circuit_2_z, n);
  and and_7 (out_11, decoder_circuit_2_u, n);
  and and_8 (out_7, decoder_circuit_1_u, ~n);  // AND_Gate
endmodule

module seven_code_trans (
  input  m0,
  input  m1,
  input  m2,
  input  m3,
  output a,
  output b,
  output c,
  output d,
  output e,
  output f,
  output g,
  output h
);

  wire decoder_1_out0, decoder_1_out1, decoder_1_out2, decoder_1_out3, decoder_1_out4, decoder_1_out5,
       decoder_1_out6, decoder_1_out7, decoder_1_out8, decoder_1_out9, decoder_1_out10, decoder_1_out11,
       decoder_1_out12, decoder_1_out13, decoder_1_out14, decoder_1_out15;

  Decoder #(.select(4)) decoder_1 (
    .out0(decoder_1_out0), .out1(decoder_1_out1), .out2(decoder_1_out2), .out3(decoder_1_out3),
    .out4(decoder_1_out4), .out5(decoder_1_out5), .out6(decoder_1_out6), .out7(decoder_1_out7),
    .out8(decoder_1_out8), .out9(decoder_1_out9), .out10(decoder_1_out10), .out11(decoder_1_out11),
    .out12(decoder_1_out12), .out13(decoder_1_out13), .out14(decoder_1_out14), .out15(decoder_1_out15),
    .sel({m3, m2, m1, m0}), .en(1'b1));
  or or_1 (a, decoder_1_out2, decoder_1_out3, decoder_1_out4, decoder_1_out5, decoder_1_out6, decoder_1_out8, decoder_1_out9);
  _7_Segment_Display u_7_segment_display_1 (.g(a), .f(b), .a(c), .b(d), .e(e), .d(f), .c(g), .dp(h));
  or or_2 (b, decoder_1_out0, decoder_1_out4, decoder_1_out5, decoder_1_out6, decoder_1_out8, decoder_1_out9);
  or or_3 (c, decoder_1_out0, decoder_1_out2, decoder_1_out3, decoder_1_out5, decoder_1_out6, decoder_1_out7, decoder_1_out8, decoder_1_out9);
  or or_4 (d, decoder_1_out0, decoder_1_out1, decoder_1_out2, decoder_1_out3, decoder_1_out7, decoder_1_out8, decoder_1_out9, decoder_1_out4);
  or or_5 (e, decoder_1_out0, decoder_1_out2, decoder_1_out6, decoder_1_out8);
  or or_6 (f, decoder_1_out0, decoder_1_out3, decoder_1_out9, decoder_1_out2, decoder_1_out5, decoder_1_out6, decoder_1_out8);
  or or_7 (g, decoder_1_out0, decoder_1_out1, decoder_1_out4, decoder_1_out3, decoder_1_out5, decoder_1_out6, decoder_1_out7, decoder_1_out8, decoder_1_out9);
  or or_8 (h, decoder_1_out13, decoder_1_out12, decoder_1_out11, decoder_1_out10, decoder_1_out14, decoder_1_out15);

  // Notes on the sheet:
  //   1
  //   8
  //   1
  //   2
  //   3
  //   4
  //   5
  //   6
  //   7
endmodule

module seven_code_16_trans (
  input  m0,
  input  m1,
  input  m2,
  input  m3,
  output a,
  output b,
  output c,
  output d,
  output e,
  output f,
  output g,
  output h
);

  wire decoder_1_out0, decoder_1_out1, decoder_1_out2, decoder_1_out3, decoder_1_out4, decoder_1_out5,
       decoder_1_out6, decoder_1_out7, decoder_1_out8, decoder_1_out9, decoder_1_out10, decoder_1_out11,
       decoder_1_out12, decoder_1_out13, decoder_1_out14, decoder_1_out15;

  Decoder #(.select(4)) decoder_1 (
    .out0(decoder_1_out0), .out1(decoder_1_out1), .out2(decoder_1_out2), .out3(decoder_1_out3),
    .out4(decoder_1_out4), .out5(decoder_1_out5), .out6(decoder_1_out6), .out7(decoder_1_out7),
    .out8(decoder_1_out8), .out9(decoder_1_out9), .out10(decoder_1_out10), .out11(decoder_1_out11),
    .out12(decoder_1_out12), .out13(decoder_1_out13), .out14(decoder_1_out14), .out15(decoder_1_out15),
    .sel({m3, m2, m1, m0}), .en(1'b1));
  or or_1 (d, decoder_1_out10, decoder_1_out0, decoder_1_out1, decoder_1_out2, decoder_1_out3, decoder_1_out7, decoder_1_out8, decoder_1_out9, decoder_1_out4, decoder_1_out13);
  or or_2 (a, decoder_1_out10, decoder_1_out11, decoder_1_out5, decoder_1_out2, decoder_1_out3, decoder_1_out4, decoder_1_out6, decoder_1_out8, decoder_1_out9, decoder_1_out13, decoder_1_out14, decoder_1_out15);
  _7_Segment_Display u_7_segment_display_1 (.g(a), .f(b), .a(c), .b(d), .e(e), .d(f), .c(g));  // open: dp
  or or_3 (g, decoder_1_out10, decoder_1_out5, decoder_1_out0, decoder_1_out1, decoder_1_out4, decoder_1_out3, decoder_1_out6, decoder_1_out7, decoder_1_out8, decoder_1_out9, decoder_1_out11, decoder_1_out13);
  or or_4 (f, decoder_1_out14, decoder_1_out13, decoder_1_out0, decoder_1_out3, decoder_1_out9, decoder_1_out2, decoder_1_out5, decoder_1_out6, decoder_1_out8, decoder_1_out12, decoder_1_out11);
  or or_5 (b, decoder_1_out10, decoder_1_out11, decoder_1_out0, decoder_1_out4, decoder_1_out5, decoder_1_out12, decoder_1_out6, decoder_1_out8, decoder_1_out9, decoder_1_out15, decoder_1_out14);
  or or_6 (c, decoder_1_out14, decoder_1_out15, decoder_1_out0, decoder_1_out2, decoder_1_out3, decoder_1_out5, decoder_1_out6, decoder_1_out7, decoder_1_out8, decoder_1_out10, decoder_1_out12, decoder_1_out9);
  or or_7 (e, decoder_1_out15, decoder_1_out14, decoder_1_out13, decoder_1_out0, decoder_1_out2, decoder_1_out6, decoder_1_out8, decoder_1_out12, decoder_1_out11, decoder_1_out10);

  // Notes on the sheet:
  //   1
  //   1
  //   2
  //   3
  //   4
  //   5
  //   6
  //   7
endmodule

module encoder (
);

  wire dipswitch_1_sw2, dipswitch_1_sw3, dipswitch_1_sw4, dipswitch_1_sw5, dipswitch_1_sw6, dipswitch_1_sw7,
       dipswitch_1_sw8, dipswitch_1_sw9, dipswitch_1_sw10, dipswitch_1_sw11, dipswitch_1_sw12,
       dipswitch_1_sw13, dipswitch_1_sw14, dipswitch_1_sw15, dipswitch_1_sw16, or_1_out, or_2_out, or_3_out,
       or_4_out, seven_code_16_trans_1_a, seven_code_16_trans_1_b, seven_code_16_trans_1_c,
       seven_code_16_trans_1_d, seven_code_16_trans_1_e, seven_code_16_trans_1_f, seven_code_16_trans_1_g;

  DipSwitch #(.number(16)) dipswitch_1 (
    .sw2(dipswitch_1_sw2), .sw3(dipswitch_1_sw3), .sw4(dipswitch_1_sw4), .sw5(dipswitch_1_sw5),
    .sw6(dipswitch_1_sw6), .sw7(dipswitch_1_sw7), .sw8(dipswitch_1_sw8), .sw9(dipswitch_1_sw9),
    .sw10(dipswitch_1_sw10), .sw11(dipswitch_1_sw11), .sw12(dipswitch_1_sw12), .sw13(dipswitch_1_sw13),
    .sw14(dipswitch_1_sw14), .sw15(dipswitch_1_sw15), .sw16(dipswitch_1_sw16));  // open: sw1
  or or_1 (or_1_out, dipswitch_1_sw2, dipswitch_1_sw4, dipswitch_1_sw6, dipswitch_1_sw8, dipswitch_1_sw10, dipswitch_1_sw12, dipswitch_1_sw14, dipswitch_1_sw16);
  or or_2 (or_2_out, dipswitch_1_sw3, dipswitch_1_sw4, dipswitch_1_sw7, dipswitch_1_sw8, dipswitch_1_sw11, dipswitch_1_sw12, dipswitch_1_sw15, dipswitch_1_sw16);
  or or_3 (or_3_out, dipswitch_1_sw5, dipswitch_1_sw6, dipswitch_1_sw7, dipswitch_1_sw8, dipswitch_1_sw13, dipswitch_1_sw14, dipswitch_1_sw15, dipswitch_1_sw16);
  or or_4 (or_4_out, dipswitch_1_sw9, dipswitch_1_sw10, dipswitch_1_sw11, dipswitch_1_sw12, dipswitch_1_sw13, dipswitch_1_sw14, dipswitch_1_sw15, dipswitch_1_sw16);
  seven_code_16_trans seven_code_16_trans_1 (
    .m0(or_1_out), .m1(or_2_out), .m2(or_3_out), .m3(or_4_out), .a(seven_code_16_trans_1_a),
    .b(seven_code_16_trans_1_b), .c(seven_code_16_trans_1_c), .d(seven_code_16_trans_1_d),
    .e(seven_code_16_trans_1_e), .f(seven_code_16_trans_1_f), .g(seven_code_16_trans_1_g));  // open: h
  _7_Segment_Display u_7_segment_display_1 (
    .g(seven_code_16_trans_1_a), .f(seven_code_16_trans_1_b), .a(seven_code_16_trans_1_c),
    .b(seven_code_16_trans_1_d), .e(seven_code_16_trans_1_e), .d(seven_code_16_trans_1_f),
    .c(seven_code_16_trans_1_g));  // open: dp

  // Notes on the sheet:
  //   0
  //   15
endmodule

module encoder_privil (
  input  A0,
  input  A1,
  input  A2,
  input  A3,
  output Y0,
  output Y1
);

  wire and_1_out, and_2_out, seven_code_16_trans_1_a, seven_code_16_trans_1_b, seven_code_16_trans_1_c,
       seven_code_16_trans_1_d, seven_code_16_trans_1_e, seven_code_16_trans_1_f, seven_code_16_trans_1_g;

  or or_1 (Y0, A3, and_1_out);
  and and_1 (and_1_out, A1, ~A2, ~A3);  // AND_Gate
  or or_2 (Y1, A3, and_2_out);
  and and_2 (and_2_out, ~A3, A2);  // AND_Gate
  seven_code_16_trans seven_code_16_trans_1 (
    .m0(Y0), .m1(Y1), .m2(1'b0), .m3(1'b0), .a(seven_code_16_trans_1_a), .b(seven_code_16_trans_1_b),
    .c(seven_code_16_trans_1_c), .d(seven_code_16_trans_1_d), .e(seven_code_16_trans_1_e),
    .f(seven_code_16_trans_1_f), .g(seven_code_16_trans_1_g));  // open: h
  _7_Segment_Display u_7_segment_display_1 (
    .g(seven_code_16_trans_1_a), .f(seven_code_16_trans_1_b), .a(seven_code_16_trans_1_c),
    .b(seven_code_16_trans_1_d), .e(seven_code_16_trans_1_e), .d(seven_code_16_trans_1_f),
    .c(seven_code_16_trans_1_g));  // open: dp
endmodule

module encoder_16to4 (
);

  wire dipswitch_1_sw1, dipswitch_1_sw2, dipswitch_1_sw3, dipswitch_1_sw4, dipswitch_1_sw5, dipswitch_1_sw6,
       dipswitch_1_sw7, dipswitch_1_sw8, dipswitch_1_sw9, dipswitch_1_sw10, dipswitch_1_sw11,
       dipswitch_1_sw12, dipswitch_1_sw13, dipswitch_1_sw14, dipswitch_1_sw15, dipswitch_1_sw16,
       encoder_privil_1_y0, encoder_privil_1_y1, encoder_privil_2_y0, encoder_privil_2_y1,
       encoder_privil_3_y0, encoder_privil_3_y1, encoder_privil_4_y0, encoder_privil_4_y1,
       encoder_privil_5_y0, encoder_privil_5_y1, encoder_privil_6_y0, encoder_privil_6_y1,
       encoder_privil_7_y0, encoder_privil_7_y1, encoder_privil_8_y0, encoder_privil_8_y1, or_1_out,
       or_2_out, or_3_out, or_4_out, seven_code_16_trans_1_a, seven_code_16_trans_1_b,
       seven_code_16_trans_1_c, seven_code_16_trans_1_d, seven_code_16_trans_1_e, seven_code_16_trans_1_f,
       seven_code_16_trans_1_g;

  DipSwitch #(.number(16)) dipswitch_1 (
    .sw1(dipswitch_1_sw1), .sw2(dipswitch_1_sw2), .sw3(dipswitch_1_sw3), .sw4(dipswitch_1_sw4),
    .sw5(dipswitch_1_sw5), .sw6(dipswitch_1_sw6), .sw7(dipswitch_1_sw7), .sw8(dipswitch_1_sw8),
    .sw9(dipswitch_1_sw9), .sw10(dipswitch_1_sw10), .sw11(dipswitch_1_sw11), .sw12(dipswitch_1_sw12),
    .sw13(dipswitch_1_sw13), .sw14(dipswitch_1_sw14), .sw15(dipswitch_1_sw15), .sw16(dipswitch_1_sw16));
  or or_1 (or_1_out, dipswitch_1_sw1, dipswitch_1_sw2, dipswitch_1_sw3, dipswitch_1_sw4);
  or or_2 (or_2_out, dipswitch_1_sw5, dipswitch_1_sw6, dipswitch_1_sw7, dipswitch_1_sw8);
  or or_3 (or_3_out, dipswitch_1_sw9, dipswitch_1_sw10, dipswitch_1_sw11, dipswitch_1_sw12);
  or or_4 (or_4_out, dipswitch_1_sw13, dipswitch_1_sw14, dipswitch_1_sw15, dipswitch_1_sw16);
  encoder_privil encoder_privil_1 (
    .A0(dipswitch_1_sw1), .A1(dipswitch_1_sw2), .A2(dipswitch_1_sw3), .A3(dipswitch_1_sw4),
    .Y0(encoder_privil_1_y0), .Y1(encoder_privil_1_y1));
  encoder_privil encoder_privil_2 (
    .A0(dipswitch_1_sw5), .A1(dipswitch_1_sw6), .A2(dipswitch_1_sw7), .A3(dipswitch_1_sw8),
    .Y0(encoder_privil_2_y0), .Y1(encoder_privil_2_y1));
  encoder_privil encoder_privil_3 (
    .A0(or_1_out), .A1(or_2_out), .A2(or_3_out), .A3(or_4_out), .Y0(encoder_privil_3_y0),
    .Y1(encoder_privil_3_y1));
  encoder_privil encoder_privil_4 (
    .A0(encoder_privil_1_y0), .A1(encoder_privil_1_y1), .A2(encoder_privil_2_y0), .A3(encoder_privil_2_y1),
    .Y0(encoder_privil_4_y0), .Y1(encoder_privil_4_y1));
  encoder_privil encoder_privil_5 (
    .A0(dipswitch_1_sw9), .A1(dipswitch_1_sw10), .A2(dipswitch_1_sw11), .A3(dipswitch_1_sw12),
    .Y0(encoder_privil_5_y0), .Y1(encoder_privil_5_y1));
  encoder_privil encoder_privil_6 (
    .A0(encoder_privil_4_y0), .A1(encoder_privil_4_y1), .A2(encoder_privil_5_y0), .A3(encoder_privil_5_y1),
    .Y0(encoder_privil_6_y0), .Y1(encoder_privil_6_y1));
  encoder_privil encoder_privil_7 (
    .A0(dipswitch_1_sw13), .A1(dipswitch_1_sw14), .A2(dipswitch_1_sw15), .A3(dipswitch_1_sw16),
    .Y0(encoder_privil_7_y0), .Y1(encoder_privil_7_y1));
  encoder_privil encoder_privil_8 (
    .A0(encoder_privil_6_y0), .A1(encoder_privil_6_y1), .A2(encoder_privil_7_y0), .A3(encoder_privil_7_y1),
    .Y0(encoder_privil_8_y0), .Y1(encoder_privil_8_y1));
  seven_code_16_trans seven_code_16_trans_1 (
    .m0(encoder_privil_8_y0), .m1(encoder_privil_8_y1), .m2(encoder_privil_3_y0), .m3(encoder_privil_3_y1),
    .a(seven_code_16_trans_1_a), .b(seven_code_16_trans_1_b), .c(seven_code_16_trans_1_c),
    .d(seven_code_16_trans_1_d), .e(seven_code_16_trans_1_e), .f(seven_code_16_trans_1_f),
    .g(seven_code_16_trans_1_g));  // open: h
  _7_Segment_Display u_7_segment_display_1 (
    .g(seven_code_16_trans_1_a), .f(seven_code_16_trans_1_b), .a(seven_code_16_trans_1_c),
    .b(seven_code_16_trans_1_d), .e(seven_code_16_trans_1_e), .d(seven_code_16_trans_1_f),
    .c(seven_code_16_trans_1_g));  // open: dp
endmodule

module encoder_16to4_true (
);

  wire and_1_out, and_2_out, and_3_out, and_4_out, and_5_out, and_6_out, dipswitch_1_sw1, dipswitch_1_sw2,
       dipswitch_1_sw3, dipswitch_1_sw4, dipswitch_1_sw5, dipswitch_1_sw6, dipswitch_1_sw7, dipswitch_1_sw8,
       dipswitch_1_sw9, dipswitch_1_sw10, dipswitch_1_sw11, dipswitch_1_sw12, dipswitch_1_sw13,
       dipswitch_1_sw14, dipswitch_1_sw15, dipswitch_1_sw16, encoder_privil_1_y0, encoder_privil_1_y1,
       encoder_privil_2_y0, encoder_privil_2_y1, encoder_privil_3_y0, encoder_privil_3_y1,
       encoder_privil_4_y0, encoder_privil_4_y1, encoder_privil_5_y0, encoder_privil_5_y1, or_1_out,
       or_2_out, or_3_out, or_4_out, or_5_out, or_6_out, seven_code_16_trans_1_a, seven_code_16_trans_1_b,
       seven_code_16_trans_1_c, seven_code_16_trans_1_d, seven_code_16_trans_1_e, seven_code_16_trans_1_f,
       seven_code_16_trans_1_g;

  DipSwitch #(.number(16)) dipswitch_1 (
    .sw1(dipswitch_1_sw1), .sw2(dipswitch_1_sw2), .sw3(dipswitch_1_sw3), .sw4(dipswitch_1_sw4),
    .sw5(dipswitch_1_sw5), .sw6(dipswitch_1_sw6), .sw7(dipswitch_1_sw7), .sw8(dipswitch_1_sw8),
    .sw9(dipswitch_1_sw9), .sw10(dipswitch_1_sw10), .sw11(dipswitch_1_sw11), .sw12(dipswitch_1_sw12),
    .sw13(dipswitch_1_sw13), .sw14(dipswitch_1_sw14), .sw15(dipswitch_1_sw15), .sw16(dipswitch_1_sw16));
  or or_1 (or_1_out, dipswitch_1_sw1, dipswitch_1_sw2, dipswitch_1_sw3, dipswitch_1_sw4);
  or or_2 (or_2_out, dipswitch_1_sw5, dipswitch_1_sw6, dipswitch_1_sw7, dipswitch_1_sw8);
  or or_3 (or_3_out, dipswitch_1_sw9, dipswitch_1_sw10, dipswitch_1_sw11, dipswitch_1_sw12);
  or or_4 (or_4_out, dipswitch_1_sw13, dipswitch_1_sw14, dipswitch_1_sw15, dipswitch_1_sw16);
  encoder_privil encoder_privil_1 (
    .A0(dipswitch_1_sw1), .A1(dipswitch_1_sw2), .A2(dipswitch_1_sw3), .A3(dipswitch_1_sw4),
    .Y0(encoder_privil_1_y0), .Y1(encoder_privil_1_y1));
  encoder_privil encoder_privil_2 (
    .A0(dipswitch_1_sw5), .A1(dipswitch_1_sw6), .A2(dipswitch_1_sw7), .A3(dipswitch_1_sw8),
    .Y0(encoder_privil_2_y0), .Y1(encoder_privil_2_y1));
  encoder_privil encoder_privil_3 (
    .A0(dipswitch_1_sw9), .A1(dipswitch_1_sw10), .A2(dipswitch_1_sw11), .A3(dipswitch_1_sw12),
    .Y0(encoder_privil_3_y0), .Y1(encoder_privil_3_y1));
  encoder_privil encoder_privil_4 (
    .A0(dipswitch_1_sw13), .A1(dipswitch_1_sw14), .A2(dipswitch_1_sw15), .A3(dipswitch_1_sw16),
    .Y0(encoder_privil_4_y0), .Y1(encoder_privil_4_y1));
  encoder_privil encoder_privil_5 (
    .A0(or_1_out), .A1(or_2_out), .A2(or_3_out), .A3(or_4_out), .Y0(encoder_privil_5_y0),
    .Y1(encoder_privil_5_y1));
  and and_1 (and_1_out, encoder_privil_1_y0, ~encoder_privil_2_y0, ~encoder_privil_2_y1, ~encoder_privil_3_y0, ~encoder_privil_3_y1, ~encoder_privil_4_y0, ~encoder_privil_4_y1);  // AND_Gate
  and and_2 (and_2_out, encoder_privil_1_y1, ~encoder_privil_2_y0, ~encoder_privil_2_y1, ~encoder_privil_3_y0, ~encoder_privil_3_y1, ~encoder_privil_4_y0, ~encoder_privil_4_y1);  // AND_Gate
  and and_3 (and_3_out, encoder_privil_2_y0, ~encoder_privil_3_y0, ~encoder_privil_3_y1, ~encoder_privil_4_y0, ~encoder_privil_4_y1);  // AND_Gate
  and and_4 (and_4_out, encoder_privil_2_y1, ~encoder_privil_3_y0, ~encoder_privil_3_y1, ~encoder_privil_4_y0, ~encoder_privil_4_y1);  // AND_Gate
  and and_5 (and_5_out, encoder_privil_3_y0, ~encoder_privil_4_y0, ~encoder_privil_4_y1);  // AND_Gate
  and and_6 (and_6_out, encoder_privil_3_y1, ~encoder_privil_4_y0, ~encoder_privil_4_y1);  // AND_Gate
  or or_5 (or_5_out, and_1_out, and_3_out, and_5_out, encoder_privil_4_y0);
  or or_6 (or_6_out, and_2_out, and_4_out, and_6_out, encoder_privil_4_y1);
  _7_Segment_Display u_7_segment_display_1 (
    .g(seven_code_16_trans_1_a), .f(seven_code_16_trans_1_b), .a(seven_code_16_trans_1_c),
    .b(seven_code_16_trans_1_d), .e(seven_code_16_trans_1_e), .d(seven_code_16_trans_1_f),
    .c(seven_code_16_trans_1_g));  // open: dp
  seven_code_16_trans seven_code_16_trans_1 (
    .m0(or_5_out), .m1(or_6_out), .m2(encoder_privil_5_y0), .m3(encoder_privil_5_y1),
    .a(seven_code_16_trans_1_a), .b(seven_code_16_trans_1_b), .c(seven_code_16_trans_1_c),
    .d(seven_code_16_trans_1_d), .e(seven_code_16_trans_1_e), .f(seven_code_16_trans_1_f),
    .g(seven_code_16_trans_1_g), .h(seven_code_16_trans_1_g));
endmodule

module encoder_16to4_true1 (
);

  wire and_1_out, and_2_out, and_3_out, and_4_out, and_5_out, and_6_out, and_7_out, and_8_out,
       dipswitch_1_sw1, dipswitch_1_sw2, dipswitch_1_sw3, dipswitch_1_sw4, dipswitch_1_sw5, dipswitch_1_sw6,
       dipswitch_1_sw7, dipswitch_1_sw8, dipswitch_1_sw9, dipswitch_1_sw10, dipswitch_1_sw11,
       dipswitch_1_sw12, dipswitch_1_sw13, dipswitch_1_sw14, dipswitch_1_sw15, dipswitch_1_sw16,
       encoder_privil_1_y0, encoder_privil_1_y1, encoder_privil_2_y0, encoder_privil_2_y1,
       encoder_privil_3_y0, encoder_privil_3_y1, encoder_privil_4_y0, encoder_privil_4_y1,
       encoder_privil_5_y0, encoder_privil_5_y1, or_1_out, or_2_out, or_3_out, or_4_out, or_5_out, or_6_out,
       seven_code_16_trans_1_a, seven_code_16_trans_1_b, seven_code_16_trans_1_c, seven_code_16_trans_1_d,
       seven_code_16_trans_1_e, seven_code_16_trans_1_f, seven_code_16_trans_1_g;

  DipSwitch #(.number(16)) dipswitch_1 (
    .sw1(dipswitch_1_sw1), .sw2(dipswitch_1_sw2), .sw3(dipswitch_1_sw3), .sw4(dipswitch_1_sw4),
    .sw5(dipswitch_1_sw5), .sw6(dipswitch_1_sw6), .sw7(dipswitch_1_sw7), .sw8(dipswitch_1_sw8),
    .sw9(dipswitch_1_sw9), .sw10(dipswitch_1_sw10), .sw11(dipswitch_1_sw11), .sw12(dipswitch_1_sw12),
    .sw13(dipswitch_1_sw13), .sw14(dipswitch_1_sw14), .sw15(dipswitch_1_sw15), .sw16(dipswitch_1_sw16));
  or or_1 (or_1_out, dipswitch_1_sw1, dipswitch_1_sw2, dipswitch_1_sw3, dipswitch_1_sw4);
  or or_2 (or_2_out, dipswitch_1_sw5, dipswitch_1_sw6, dipswitch_1_sw7, dipswitch_1_sw8);
  or or_3 (or_3_out, dipswitch_1_sw9, dipswitch_1_sw10, dipswitch_1_sw11, dipswitch_1_sw12);
  or or_4 (or_4_out, dipswitch_1_sw13, dipswitch_1_sw14, dipswitch_1_sw15, dipswitch_1_sw16);
  encoder_privil encoder_privil_1 (
    .A0(dipswitch_1_sw1), .A1(dipswitch_1_sw2), .A2(dipswitch_1_sw3), .A3(dipswitch_1_sw4),
    .Y0(encoder_privil_1_y0), .Y1(encoder_privil_1_y1));
  encoder_privil encoder_privil_2 (
    .A0(dipswitch_1_sw5), .A1(dipswitch_1_sw6), .A2(dipswitch_1_sw7), .A3(dipswitch_1_sw8),
    .Y0(encoder_privil_2_y0), .Y1(encoder_privil_2_y1));
  encoder_privil encoder_privil_3 (
    .A0(dipswitch_1_sw9), .A1(dipswitch_1_sw10), .A2(dipswitch_1_sw11), .A3(dipswitch_1_sw12),
    .Y0(encoder_privil_3_y0), .Y1(encoder_privil_3_y1));
  encoder_privil encoder_privil_4 (
    .A0(dipswitch_1_sw13), .A1(dipswitch_1_sw14), .A2(dipswitch_1_sw15), .A3(dipswitch_1_sw16),
    .Y0(encoder_privil_4_y0), .Y1(encoder_privil_4_y1));
  and and_1 (and_1_out, encoder_privil_1_y0, or_1_out, ~or_2_out, ~or_3_out, ~or_4_out);  // AND_Gate
  encoder_privil encoder_privil_5 (
    .A0(or_1_out), .A1(or_2_out), .A2(or_3_out), .A3(or_4_out), .Y0(encoder_privil_5_y0),
    .Y1(encoder_privil_5_y1));
  and and_2 (and_2_out, encoder_privil_1_y1, or_1_out, ~or_2_out, ~or_3_out, ~or_4_out);  // AND_Gate
  and and_3 (and_3_out, encoder_privil_2_y0, or_2_out, ~or_3_out, ~or_4_out);  // AND_Gate
  and and_4 (and_4_out, encoder_privil_2_y1, or_2_out, ~or_3_out, ~or_4_out);  // AND_Gate
  and and_5 (and_5_out, encoder_privil_3_y0, or_3_out, ~or_4_out);  // AND_Gate
  and and_6 (and_6_out, encoder_privil_3_y1, or_3_out, ~or_4_out);  // AND_Gate
  or or_5 (or_5_out, and_1_out, and_3_out, and_5_out, and_7_out);
  and and_7 (and_7_out, encoder_privil_4_y0, or_4_out);
  and and_8 (and_8_out, encoder_privil_4_y1, or_4_out);
  or or_6 (or_6_out, and_2_out, and_4_out, and_6_out, and_8_out);
  _7_Segment_Display u_7_segment_display_1 (
    .g(seven_code_16_trans_1_a), .f(seven_code_16_trans_1_b), .a(seven_code_16_trans_1_c),
    .b(seven_code_16_trans_1_d), .e(seven_code_16_trans_1_e), .d(seven_code_16_trans_1_f),
    .c(seven_code_16_trans_1_g));  // open: dp
  seven_code_16_trans seven_code_16_trans_1 (
    .m0(or_5_out), .m1(or_6_out), .m2(encoder_privil_5_y0), .m3(encoder_privil_5_y1),
    .a(seven_code_16_trans_1_a), .b(seven_code_16_trans_1_b), .c(seven_code_16_trans_1_c),
    .d(seven_code_16_trans_1_d), .e(seven_code_16_trans_1_e), .f(seven_code_16_trans_1_f),
    .g(seven_code_16_trans_1_g), .h(seven_code_16_trans_1_g));
endmodule

module encoder_16to4_gemini (
);

  wire and_2_out, and_3_out, and_4_out, and_6_out, and_8_out, dipswitch_1_sw1, dipswitch_1_sw2,
       dipswitch_1_sw3, dipswitch_1_sw4, dipswitch_1_sw5, dipswitch_1_sw6, dipswitch_1_sw7, dipswitch_1_sw8,
       dipswitch_1_sw9, dipswitch_1_sw10, dipswitch_1_sw11, dipswitch_1_sw12, dipswitch_1_sw13,
       dipswitch_1_sw14, dipswitch_1_sw15, dipswitch_1_sw16, encoder_privil_1_y0, encoder_privil_1_y1,
       encoder_privil_2_y0, encoder_privil_2_y1, encoder_privil_3_y0, encoder_privil_3_y1,
       encoder_privil_4_y0, encoder_privil_4_y1, encoder_privil_5_y0, encoder_privil_5_y1, not_1_out,
       or_1_out, or_2_out, or_4_out, or_5_out, or_6_out, seven_code_16_trans_1_a, seven_code_16_trans_1_b,
       seven_code_16_trans_1_c, seven_code_16_trans_1_d, seven_code_16_trans_1_e, seven_code_16_trans_1_f,
       seven_code_16_trans_1_g;

  DipSwitch #(.number(16)) dipswitch_1 (
    .sw1(dipswitch_1_sw1), .sw2(dipswitch_1_sw2), .sw3(dipswitch_1_sw3), .sw4(dipswitch_1_sw4),
    .sw5(dipswitch_1_sw5), .sw6(dipswitch_1_sw6), .sw7(dipswitch_1_sw7), .sw8(dipswitch_1_sw8),
    .sw9(dipswitch_1_sw9), .sw10(dipswitch_1_sw10), .sw11(dipswitch_1_sw11), .sw12(dipswitch_1_sw12),
    .sw13(dipswitch_1_sw13), .sw14(dipswitch_1_sw14), .sw15(dipswitch_1_sw15), .sw16(dipswitch_1_sw16));
  or or_1 (or_1_out, dipswitch_1_sw1, dipswitch_1_sw2, dipswitch_1_sw3, dipswitch_1_sw4);
  or or_2 (or_2_out, dipswitch_1_sw5, dipswitch_1_sw6, dipswitch_1_sw7, dipswitch_1_sw8);
  or or_3 (or_2_out, dipswitch_1_sw9, dipswitch_1_sw10, dipswitch_1_sw11, dipswitch_1_sw12);
  or or_4 (or_4_out, dipswitch_1_sw13, dipswitch_1_sw14, dipswitch_1_sw15, dipswitch_1_sw16);
  encoder_privil encoder_privil_1 (
    .A0(dipswitch_1_sw1), .A1(dipswitch_1_sw2), .A2(dipswitch_1_sw3), .A3(dipswitch_1_sw4),
    .Y0(encoder_privil_1_y0), .Y1(encoder_privil_1_y1));
  encoder_privil encoder_privil_2 (
    .A0(dipswitch_1_sw5), .A1(dipswitch_1_sw6), .A2(dipswitch_1_sw7), .A3(dipswitch_1_sw8),
    .Y0(encoder_privil_2_y0), .Y1(encoder_privil_2_y1));
  encoder_privil encoder_privil_3 (
    .A0(dipswitch_1_sw9), .A1(dipswitch_1_sw10), .A2(dipswitch_1_sw11), .A3(dipswitch_1_sw12),
    .Y0(encoder_privil_3_y0), .Y1(encoder_privil_3_y1));
  encoder_privil encoder_privil_4 (
    .A0(dipswitch_1_sw13), .A1(dipswitch_1_sw14), .A2(dipswitch_1_sw15), .A3(dipswitch_1_sw16),
    .Y0(encoder_privil_4_y0), .Y1(encoder_privil_4_y1));
  not not_1 (not_1_out, or_4_out);
  and and_1 (or_2_out, not_1_out, ~or_2_out);  // AND_Gate
  encoder_privil encoder_privil_5 (
    .A0(or_1_out), .A1(or_2_out), .A2(or_2_out), .A3(or_4_out), .Y0(encoder_privil_5_y0),
    .Y1(encoder_privil_5_y1));
  and and_2 (and_2_out, or_2_out, ~or_2_out);  // AND_Gate
  and and_3 (and_3_out, encoder_privil_1_y0, and_2_out);
  and and_4 (and_4_out, encoder_privil_1_y1, and_2_out);
  and and_5 (encoder_privil_4_y0, encoder_privil_2_y0, or_2_out);
  and and_6 (and_6_out, encoder_privil_2_y1, or_2_out);
  and and_7 (encoder_privil_4_y0, encoder_privil_3_y0, not_1_out);
  and and_8 (and_8_out, encoder_privil_3_y1, not_1_out);
  or or_5 (or_5_out, and_3_out, encoder_privil_4_y0, encoder_privil_4_y0, encoder_privil_4_y0);
  or or_6 (or_6_out, and_4_out, and_6_out, and_8_out, encoder_privil_4_y1);
  _7_Segment_Display u_7_segment_display_1 (
    .g(seven_code_16_trans_1_a), .f(seven_code_16_trans_1_b), .a(seven_code_16_trans_1_c),
    .b(seven_code_16_trans_1_d), .e(seven_code_16_trans_1_e), .d(seven_code_16_trans_1_f),
    .c(seven_code_16_trans_1_g));  // open: dp
  seven_code_16_trans seven_code_16_trans_1 (
    .m0(or_5_out), .m1(or_6_out), .m2(encoder_privil_5_y0), .m3(encoder_privil_5_y1),
    .a(seven_code_16_trans_1_a), .b(seven_code_16_trans_1_b), .c(seven_code_16_trans_1_c),
    .d(seven_code_16_trans_1_d), .e(seven_code_16_trans_1_e), .f(seven_code_16_trans_1_f),
    .g(seven_code_16_trans_1_g), .h(seven_code_16_trans_1_g));
endmodule

module mux1 (
  input  D0,
  input  D1,
  input  S,
  output Y
);

  wire and_1_out, and_2_out, decoder_1_out0, decoder_1_out1;

  Decoder decoder_1 (.out0(decoder_1_out0), .out1(decoder_1_out1), .sel(S), .en(1'b1));
  and and_1 (and_1_out, D0, decoder_1_out0);
  and and_2 (and_2_out, decoder_1_out1, D1);
  or or_1 (Y, and_1_out, and_2_out);
endmodule

module MUX_3bit_4to1 (
  input  [2:0] D0,
  input  [2:0] D1,
  input  [1:0] S,
  input  [2:0] D2,
  input  [2:0] D3,
  output [2:0] out_6
);

  wire and_1_out, and_2_out, and_3_out, and_4_out, and_5_out, and_6_out, and_7_out, and_8_out, and_9_out,
       and_10_out, and_11_out, and_12_out, decoder_1_out0, decoder_1_out1, decoder_1_out2, decoder_1_out3;

  Decoder #(.select(2)) decoder_1 (
    .out0(decoder_1_out0), .out1(decoder_1_out1), .out2(decoder_1_out2), .out3(decoder_1_out3), .sel(S),
    .en(1'b1));
  and and_1 (and_1_out, D0[0], decoder_1_out0);
  and and_2 (and_2_out, D1[0], decoder_1_out1);
  and and_3 (and_3_out, D2[0], decoder_1_out2);
  and and_4 (and_4_out, D3[0], decoder_1_out3);
  and and_5 (and_5_out, D0[1], decoder_1_out0);
  and and_6 (and_6_out, D1[1], decoder_1_out1);
  and and_7 (and_7_out, D2[1], decoder_1_out2);
  and and_8 (and_8_out, D3[1], decoder_1_out3);
  and and_9 (and_9_out, D0[2], decoder_1_out0);
  and and_10 (and_10_out, D1[2], decoder_1_out1);
  and and_11 (and_11_out, D2[2], decoder_1_out2);
  and and_12 (and_12_out, D3[2], decoder_1_out3);
  or or_1 (out_6[0], and_1_out, and_2_out, and_3_out, and_4_out);
  or or_2 (out_6[1], and_5_out, and_6_out, and_7_out, and_8_out);
  or or_3 (out_6[2], and_9_out, and_10_out, and_11_out, and_12_out);
endmodule

module seven_code_16or10_trans (
  input  m0,
  input  m1,
  input  m2,
  input  m3,
  input  s
);

  wire [7:0] multiplexer_1_out, seven_code_16_trans_1_a, seven_code_trans_1_a;

  seven_code_trans seven_code_trans_1 (
    .m0(m0), .m1(m1), .m2(m2), .m3(m3), .a(seven_code_trans_1_a[0]), .b(seven_code_trans_1_a[1]),
    .c(seven_code_trans_1_a[2]), .d(seven_code_trans_1_a[3]), .e(seven_code_trans_1_a[4]),
    .f(seven_code_trans_1_a[5]), .g(seven_code_trans_1_a[6]), .h(seven_code_trans_1_a[7]));
  seven_code_16_trans seven_code_16_trans_1 (
    .m0(m3), .m1(m2), .m2(m1), .m3(m0), .a(seven_code_16_trans_1_a[0]), .b(seven_code_16_trans_1_a[1]),
    .c(seven_code_16_trans_1_a[2]), .d(seven_code_16_trans_1_a[3]), .e(seven_code_16_trans_1_a[4]),
    .f(seven_code_16_trans_1_a[5]), .g(seven_code_16_trans_1_a[6]), .h(seven_code_16_trans_1_a[7]));
  Multiplexer #(.width(8)) multiplexer_1 (
    .in0(seven_code_trans_1_a), .in1(seven_code_16_trans_1_a), .out(multiplexer_1_out), .sel(s));
  _7_Segment_Display u_7_segment_display_1 (
    .g(multiplexer_1_out[0]), .f(multiplexer_1_out[1]), .a(multiplexer_1_out[2]), .b(multiplexer_1_out[3]),
    .e(multiplexer_1_out[4]), .d(multiplexer_1_out[5]), .c(multiplexer_1_out[6]), .dp(multiplexer_1_out[7]));
endmodule

module Comparator_4bit (
  input  [3:0] A,
  input  [3:0] B,
  output out_3
);

  wire xnor_1_out, xnor_2_out, xnor_3_out, xnor_4_out;

  xnor xnor_1 (xnor_1_out, A[0], B[0]);
  xnor xnor_2 (xnor_2_out, A[1], B[1]);
  xnor xnor_3 (xnor_3_out, A[2], B[2]);
  xnor xnor_4 (xnor_4_out, A[3], B[3]);
  and and_1 (out_3, xnor_1_out, xnor_2_out, xnor_3_out, xnor_4_out);
endmodule

module fulladder_1bit (
  input  A,
  input  B,
  input  Cin,
  output Cout,
  output S
);

  wire and_1_out, and_2_out, and_3_out, and_4_out, and_5_out, and_6_out, and_7_out;

  and and_1 (and_1_out, A, B);
  and and_2 (and_2_out, A, Cin);
  and and_3 (and_3_out, Cin, B);
  and and_4 (and_4_out, A, ~B, ~Cin);  // AND_Gate
  and and_5 (and_5_out, ~A, B, ~Cin);  // AND_Gate
  and and_6 (and_6_out, ~A, ~B, Cin);  // AND_Gate
  and and_7 (and_7_out, A, B, Cin);
  or or_1 (Cout, and_1_out, and_2_out, and_3_out);
  or or_2 (S, and_4_out, and_5_out, and_6_out, and_7_out);
endmodule

module halfadder_1bit (
  input  A,
  input  B,
  output S,
  output C
);

  xor xor_1 (S, A, B);
  and and_1 (C, A, B);
endmodule

module fulladder_1bit_ano (
  input  A,
  input  B,
  input  Cin,
  output S,
  output Cout
);

  wire halfadder_1bit_1_c, halfadder_1bit_1_s, halfadder_1bit_2_c;

  halfadder_1bit halfadder_1bit_1 (.A(A), .B(B), .S(halfadder_1bit_1_s), .C(halfadder_1bit_1_c));
  halfadder_1bit halfadder_1bit_2 (.A(halfadder_1bit_1_s), .B(Cin), .S(S), .C(halfadder_1bit_2_c));
  or or_1 (Cout, halfadder_1bit_1_c, halfadder_1bit_2_c);
endmodule

module adder_4bit (
  input  [3:0] A,
  input  [3:0] B,
  input  Cin,
  output [3:0] S,
  output Cout
);

  wire fulladder_1bit_ano_1_cout, fulladder_1bit_ano_2_cout, fulladder_1bit_ano_3_cout,
       seven_code_16_trans_1_a, seven_code_16_trans_1_b, seven_code_16_trans_1_c, seven_code_16_trans_1_d,
       seven_code_16_trans_1_e, seven_code_16_trans_1_f, seven_code_16_trans_1_g, seven_code_16_trans_2_a,
       seven_code_16_trans_2_b, seven_code_16_trans_2_c, seven_code_16_trans_2_d, seven_code_16_trans_2_e,
       seven_code_16_trans_2_f, seven_code_16_trans_2_g, seven_code_16_trans_3_a, seven_code_16_trans_3_b,
       seven_code_16_trans_3_c, seven_code_16_trans_3_d, seven_code_16_trans_3_e, seven_code_16_trans_3_f,
       seven_code_16_trans_3_g;

  fulladder_1bit_ano fulladder_1bit_ano_1 (.A(A[0]), .B(B[0]), .Cin(Cin), .S(S[0]), .Cout(fulladder_1bit_ano_1_cout));
  fulladder_1bit_ano fulladder_1bit_ano_2 (
    .A(A[1]), .B(B[1]), .Cin(fulladder_1bit_ano_1_cout), .S(S[1]), .Cout(fulladder_1bit_ano_2_cout));
  fulladder_1bit_ano fulladder_1bit_ano_3 (
    .A(A[2]), .B(B[2]), .Cin(fulladder_1bit_ano_2_cout), .S(S[2]), .Cout(fulladder_1bit_ano_3_cout));
  fulladder_1bit_ano fulladder_1bit_ano_4 (.A(A[3]), .B(B[3]), .Cin(fulladder_1bit_ano_3_cout), .S(S[3]), .Cout(Cout));
  LED led_1 (.in(Cout));
  seven_code_16_trans seven_code_16_trans_1 (
    .m0(A[0]), .m1(A[1]), .m2(A[2]), .m3(A[3]), .a(seven_code_16_trans_1_a), .b(seven_code_16_trans_1_b),
    .c(seven_code_16_trans_1_c), .d(seven_code_16_trans_1_d), .e(seven_code_16_trans_1_e),
    .f(seven_code_16_trans_1_f), .g(seven_code_16_trans_1_g));  // open: h
  seven_code_16_trans seven_code_16_trans_2 (
    .m0(B[0]), .m1(B[1]), .m2(B[2]), .m3(B[3]), .a(seven_code_16_trans_2_a), .b(seven_code_16_trans_2_b),
    .c(seven_code_16_trans_2_c), .d(seven_code_16_trans_2_d), .e(seven_code_16_trans_2_e),
    .f(seven_code_16_trans_2_f), .g(seven_code_16_trans_2_g));  // open: h
  _7_Segment_Display u_7_segment_display_1 (
    .g(seven_code_16_trans_1_a), .f(seven_code_16_trans_1_b), .a(seven_code_16_trans_1_c),
    .b(seven_code_16_trans_1_d), .e(seven_code_16_trans_1_e), .d(seven_code_16_trans_1_f),
    .c(seven_code_16_trans_1_g));  // open: dp
  _7_Segment_Display u_7_segment_display_2 (
    .g(seven_code_16_trans_2_a), .f(seven_code_16_trans_2_b), .a(seven_code_16_trans_2_c),
    .b(seven_code_16_trans_2_d), .e(seven_code_16_trans_2_e), .d(seven_code_16_trans_2_f),
    .c(seven_code_16_trans_2_g));  // open: dp
  _7_Segment_Display u_7_segment_display_3 (
    .g(seven_code_16_trans_3_a), .f(seven_code_16_trans_3_b), .a(seven_code_16_trans_3_c),
    .b(seven_code_16_trans_3_d), .e(seven_code_16_trans_3_e), .d(seven_code_16_trans_3_f),
    .c(seven_code_16_trans_3_g));  // open: dp
  seven_code_16_trans seven_code_16_trans_3 (
    .m0(S[0]), .m1(S[1]), .m2(S[2]), .m3(S[3]), .a(seven_code_16_trans_3_a), .b(seven_code_16_trans_3_b),
    .c(seven_code_16_trans_3_c), .d(seven_code_16_trans_3_d), .e(seven_code_16_trans_3_e),
    .f(seven_code_16_trans_3_f), .g(seven_code_16_trans_3_g));  // open: h
endmodule

module subtractor_4bit (
  input  [3:0] A,
  input  [3:0] B,
  input  Bin,
  output [3:0] D,
  output Bout
);

  wire seven_code_16_trans_1_a, seven_code_16_trans_1_b, seven_code_16_trans_1_c, seven_code_16_trans_1_d,
       seven_code_16_trans_1_e, seven_code_16_trans_1_f, seven_code_16_trans_1_g, seven_code_16_trans_2_a,
       seven_code_16_trans_2_b, seven_code_16_trans_2_c, seven_code_16_trans_2_d, seven_code_16_trans_2_e,
       seven_code_16_trans_2_f, seven_code_16_trans_2_g, seven_code_16_trans_3_a, seven_code_16_trans_3_b,
       seven_code_16_trans_3_c, seven_code_16_trans_3_d, seven_code_16_trans_3_e, seven_code_16_trans_3_f,
       seven_code_16_trans_3_g, substractor_1bit_1_bout, substractor_1bit_2_bout, substractor_1bit_3_bout;

  substractor_1bit substractor_1bit_1 (.A(A[0]), .B(B[0]), .Bin(Bin), .D(D[0]), .Bout(substractor_1bit_1_bout));
  substractor_1bit substractor_1bit_2 (
    .A(A[1]), .B(B[1]), .Bin(substractor_1bit_1_bout), .D(D[1]), .Bout(substractor_1bit_2_bout));
  substractor_1bit substractor_1bit_3 (
    .A(A[2]), .B(B[2]), .Bin(substractor_1bit_2_bout), .D(D[2]), .Bout(substractor_1bit_3_bout));
  substractor_1bit substractor_1bit_4 (.A(A[3]), .B(B[3]), .Bin(substractor_1bit_3_bout), .D(D[3]), .Bout(Bout));
  LED led_1 (.in(Bout));
  seven_code_16_trans seven_code_16_trans_1 (
    .m0(A[0]), .m1(A[1]), .m2(A[2]), .m3(A[3]), .a(seven_code_16_trans_1_a), .b(seven_code_16_trans_1_b),
    .c(seven_code_16_trans_1_c), .d(seven_code_16_trans_1_d), .e(seven_code_16_trans_1_e),
    .f(seven_code_16_trans_1_f), .g(seven_code_16_trans_1_g));  // open: h
  seven_code_16_trans seven_code_16_trans_2 (
    .m0(B[0]), .m1(B[1]), .m2(B[2]), .m3(B[3]), .a(seven_code_16_trans_2_a), .b(seven_code_16_trans_2_b),
    .c(seven_code_16_trans_2_c), .d(seven_code_16_trans_2_d), .e(seven_code_16_trans_2_e),
    .f(seven_code_16_trans_2_f), .g(seven_code_16_trans_2_g));  // open: h
  _7_Segment_Display u_7_segment_display_1 (
    .g(seven_code_16_trans_1_a), .f(seven_code_16_trans_1_b), .a(seven_code_16_trans_1_c),
    .b(seven_code_16_trans_1_d), .e(seven_code_16_trans_1_e), .d(seven_code_16_trans_1_f),
    .c(seven_code_16_trans_1_g));  // open: dp
  _7_Segment_Display u_7_segment_display_2 (
    .g(seven_code_16_trans_2_a), .f(seven_code_16_trans_2_b), .a(seven_code_16_trans_2_c),
    .b(seven_code_16_trans_2_d), .e(seven_code_16_trans_2_e), .d(seven_code_16_trans_2_f),
    .c(seven_code_16_trans_2_g));  // open: dp
  seven_code_16_trans seven_code_16_trans_3 (
    .m0(D[0]), .m1(D[1]), .m2(D[2]), .m3(D[3]), .a(seven_code_16_trans_3_a), .b(seven_code_16_trans_3_b),
    .c(seven_code_16_trans_3_c), .d(seven_code_16_trans_3_d), .e(seven_code_16_trans_3_e),
    .f(seven_code_16_trans_3_f), .g(seven_code_16_trans_3_g));  // open: h
  _7_Segment_Display u_7_segment_display_3 (
    .g(seven_code_16_trans_3_a), .f(seven_code_16_trans_3_b), .a(seven_code_16_trans_3_c),
    .b(seven_code_16_trans_3_d), .e(seven_code_16_trans_3_e), .d(seven_code_16_trans_3_f),
    .c(seven_code_16_trans_3_g));  // open: dp
endmodule

module substractor_1bit (
  input  A,
  input  B,
  input  Bin,
  output D,
  output Bout
);

  wire and_1_out, and_2_out, and_3_out, and_4_out, and_5_out;

  and and_1 (and_1_out, A, B, Bin);
  and and_2 (and_2_out, A, ~B, ~Bin);  // AND_Gate
  and and_3 (and_3_out, ~A, B, ~Bin);  // AND_Gate
  and and_4 (and_4_out, ~A, ~B, Bin);  // AND_Gate
  and and_5 (and_5_out, B, ~A, B);  // AND_Gate
  or or_1 (D, and_1_out, and_2_out, and_3_out, and_4_out);
  or or_2 (Bout, and_1_out, and_4_out, and_3_out, and_5_out);
endmodule

module SignMagnitudeAdder_4bit (
  input  [3:0] A,
  input  [3:0] B,
  output out_3,
  output [3:0] out_4
);

  wire adder_4bit_1_cout, and_1_out, and_2_out, and_3_out, and_4_out, and_5_out, or_1_out, or_2_out,
       seven_code_16_trans_1_a, seven_code_16_trans_1_b, seven_code_16_trans_1_c, seven_code_16_trans_1_d,
       seven_code_16_trans_1_e, seven_code_16_trans_1_f, seven_code_16_trans_1_g, seven_code_16_trans_2_a,
       seven_code_16_trans_2_b, seven_code_16_trans_2_c, seven_code_16_trans_2_d, seven_code_16_trans_2_e,
       seven_code_16_trans_2_f, seven_code_16_trans_2_g, seven_code_16_trans_3_a, seven_code_16_trans_3_b,
       seven_code_16_trans_3_c, seven_code_16_trans_3_d, seven_code_16_trans_3_e, seven_code_16_trans_3_f,
       seven_code_16_trans_3_g, subtractor_4bit_1_bout, xor_1_out, xor_2_out, xor_3_out;
  wire [3:0] adder_4bit_1_s, multiplexer_1_out, multiplexer_2_out, multiplexer_4_out, subtractor_4bit_1_d;
  wire [3:3] multiplexer_3_out, or_3_out;

  and and_1 (and_1_out, ~A[3], ~B[3]);  // AND_Gate
  and and_2 (and_2_out, A[3], B[3]);
  or or_1 (or_1_out, and_2_out, and_1_out);
  and and_3 (and_3_out, A[2], ~B[2]);  // AND_Gate
  xor xor_1 (xor_1_out, A[2], B[2]);
  xor xor_2 (xor_2_out, A[2], B[2]);
  and and_4 (and_4_out, ~xor_1_out, A[1], ~B[1]);  // AND_Gate
  xor xor_3 (xor_3_out, A[1], B[1]);
  and and_5 (and_5_out, ~xor_2_out, ~xor_3_out, ~A[0], B[0]);  // AND_Gate
  Multiplexer #(.width(4)) multiplexer_1 (.in0(B), .in1(A), .out(multiplexer_1_out), .sel(or_2_out));
  or or_2 (or_2_out, and_3_out, and_4_out, and_5_out);
  Multiplexer #(.width(4)) multiplexer_2 (.in0(A), .in1(B), .out(multiplexer_2_out), .sel(or_2_out));
  adder_4bit adder_4bit_1 (.A(A), .B(B), .S(adder_4bit_1_s), .Cout(adder_4bit_1_cout));  // open: Cin
  seven_code_16_trans seven_code_16_trans_1 (
    .m0(A[0]), .m1(A[1]), .m2(A[2]), .a(seven_code_16_trans_1_a), .b(seven_code_16_trans_1_b),
    .c(seven_code_16_trans_1_c), .d(seven_code_16_trans_1_d), .e(seven_code_16_trans_1_e),
    .f(seven_code_16_trans_1_f), .g(seven_code_16_trans_1_g));  // open: m3, h
  seven_code_16_trans seven_code_16_trans_2 (
    .m0(B[0]), .m1(B[1]), .m2(B[2]), .a(seven_code_16_trans_2_a), .b(seven_code_16_trans_2_b),
    .c(seven_code_16_trans_2_c), .d(seven_code_16_trans_2_d), .e(seven_code_16_trans_2_e),
    .f(seven_code_16_trans_2_f), .g(seven_code_16_trans_2_g));  // open: m3, h
  or or_3 (or_3_out[3], and_2_out, adder_4bit_1_s[3]);
  Multiplexer multiplexer_3 (.in0(B[3]), .in1(A[3]), .out(multiplexer_3_out[3]), .sel(or_2_out));
  subtractor_4bit subtractor_4bit_1 (
    .A(multiplexer_1_out), .B(multiplexer_2_out), .D(subtractor_4bit_1_d), .Bout(subtractor_4bit_1_bout));  // open: Bin
  _7_Segment_Display u_7_segment_display_1 (.g(A[3]));  // open: f, a, b, e, d, c, dp
  _7_Segment_Display u_7_segment_display_2 (
    .g(seven_code_16_trans_1_a), .f(seven_code_16_trans_1_b), .a(seven_code_16_trans_1_c),
    .b(seven_code_16_trans_1_d), .e(seven_code_16_trans_1_e), .d(seven_code_16_trans_1_f),
    .c(seven_code_16_trans_1_g));  // open: dp
  _7_Segment_Display u_7_segment_display_3 (.g(B[3]));  // open: f, a, b, e, d, c, dp
  _7_Segment_Display u_7_segment_display_4 (
    .g(seven_code_16_trans_2_a), .f(seven_code_16_trans_2_b), .a(seven_code_16_trans_2_c),
    .b(seven_code_16_trans_2_d), .e(seven_code_16_trans_2_e), .d(seven_code_16_trans_2_f),
    .c(seven_code_16_trans_2_g));  // open: dp
  Multiplexer #(.width(4)) multiplexer_4 (
    .in0({multiplexer_3_out[3], subtractor_4bit_1_d[2:0]}), .in1({or_3_out[3], adder_4bit_1_s[2:0]}),
    .out(multiplexer_4_out), .sel(or_1_out));
  or or_4 (out_3, adder_4bit_1_cout, subtractor_4bit_1_bout);
  seven_code_16_trans seven_code_16_trans_3 (
    .m0(multiplexer_4_out[0]), .m1(multiplexer_4_out[1]), .m2(multiplexer_4_out[2]),
    .a(seven_code_16_trans_3_a), .b(seven_code_16_trans_3_b), .c(seven_code_16_trans_3_c),
    .d(seven_code_16_trans_3_d), .e(seven_code_16_trans_3_e), .f(seven_code_16_trans_3_f),
    .g(seven_code_16_trans_3_g));  // open: m3, h
  _7_Segment_Display u_7_segment_display_5 (.g(multiplexer_4_out[3]));  // open: f, a, b, e, d, c, dp
  _7_Segment_Display u_7_segment_display_6 (
    .g(seven_code_16_trans_3_a), .f(seven_code_16_trans_3_b), .a(seven_code_16_trans_3_c),
    .b(seven_code_16_trans_3_d), .e(seven_code_16_trans_3_e), .d(seven_code_16_trans_3_f),
    .c(seven_code_16_trans_3_g));  // open: dp

  // Notes on the sheet:
  //   A如果比B大
  //   B符号
  //   A符号
  //   A
  //   B
  //   A
endmodule

module SMA_4bit_1 (
  input  [3:0] A,
  input  [3:0] B,
  output [3:0] Y0,
  output Y1
);

  wire and_1_out, and_2_out, and_3_out, and_4_out, and_5_out, or_1_out, or_2_out, seven_code_16_trans_1_a,
       seven_code_16_trans_1_b, seven_code_16_trans_1_c, seven_code_16_trans_1_d, seven_code_16_trans_1_e,
       seven_code_16_trans_1_f, seven_code_16_trans_1_g, seven_code_16_trans_2_a, seven_code_16_trans_2_b,
       seven_code_16_trans_2_c, seven_code_16_trans_2_d, seven_code_16_trans_2_e, seven_code_16_trans_2_f,
       seven_code_16_trans_2_g, seven_code_16_trans_3_a, seven_code_16_trans_3_b, seven_code_16_trans_3_c,
       seven_code_16_trans_3_d, seven_code_16_trans_3_e, seven_code_16_trans_3_f, seven_code_16_trans_3_g,
       xor_1_out, xor_2_out, xor_3_out;
  wire [3:0] adder_4bit_1_s, multiplexer_1_out, multiplexer_2_out, subtractor_4bit_1_d;
  wire [3:3] multiplexer_3_out;

  and and_1 (and_1_out, ~A[3], ~B[3]);  // AND_Gate
  and and_2 (and_2_out, A[3], B[3]);
  or or_1 (or_1_out, and_2_out, and_1_out);
  and and_3 (and_3_out, A[2], ~B[2]);  // AND_Gate
  xor xor_1 (xor_1_out, A[2], B[2]);
  xor xor_2 (xor_2_out, A[2], B[2]);
  and and_4 (and_4_out, ~xor_1_out, A[1], ~B[1]);  // AND_Gate
  xor xor_3 (xor_3_out, A[1], B[1]);
  and and_5 (and_5_out, ~xor_2_out, ~xor_3_out, ~A[0], B[0]);  // AND_Gate
  Multiplexer #(.width(4)) multiplexer_1 (.in0(B), .in1(A), .out(multiplexer_1_out), .sel(or_2_out));
  or or_2 (or_2_out, and_3_out, and_4_out, and_5_out);
  Multiplexer #(.width(4)) multiplexer_2 (.in0(A), .in1(B), .out(multiplexer_2_out), .sel(or_2_out));
  adder_4bit adder_4bit_1 (.A(A), .B(B), .S(adder_4bit_1_s));  // open: Cin, Cout
  seven_code_16_trans seven_code_16_trans_1 (
    .m0(A[0]), .m1(A[1]), .m2(A[2]), .a(seven_code_16_trans_1_a), .b(seven_code_16_trans_1_b),
    .c(seven_code_16_trans_1_c), .d(seven_code_16_trans_1_d), .e(seven_code_16_trans_1_e),
    .f(seven_code_16_trans_1_f), .g(seven_code_16_trans_1_g));  // open: m3, h
  seven_code_16_trans seven_code_16_trans_2 (
    .m0(B[0]), .m1(B[1]), .m2(B[2]), .a(seven_code_16_trans_2_a), .b(seven_code_16_trans_2_b),
    .c(seven_code_16_trans_2_c), .d(seven_code_16_trans_2_d), .e(seven_code_16_trans_2_e),
    .f(seven_code_16_trans_2_f), .g(seven_code_16_trans_2_g));  // open: m3, h
  Multiplexer multiplexer_3 (.in0(B[3]), .in1(A[3]), .out(multiplexer_3_out[3]), .sel(or_2_out));
  subtractor_4bit subtractor_4bit_1 (
    .A(multiplexer_1_out), .B(multiplexer_2_out), .D(subtractor_4bit_1_d));  // open: Bin, Bout
  _7_Segment_Display u_7_segment_display_1 (.g(A[3]));  // open: f, a, b, e, d, c, dp
  _7_Segment_Display u_7_segment_display_2 (
    .g(seven_code_16_trans_1_a), .f(seven_code_16_trans_1_b), .a(seven_code_16_trans_1_c),
    .b(seven_code_16_trans_1_d), .e(seven_code_16_trans_1_e), .d(seven_code_16_trans_1_f),
    .c(seven_code_16_trans_1_g));  // open: dp
  _7_Segment_Display u_7_segment_display_3 (.g(B[3]));  // open: f, a, b, e, d, c, dp
  _7_Segment_Display u_7_segment_display_4 (
    .g(seven_code_16_trans_2_a), .f(seven_code_16_trans_2_b), .a(seven_code_16_trans_2_c),
    .b(seven_code_16_trans_2_d), .e(seven_code_16_trans_2_e), .d(seven_code_16_trans_2_f),
    .c(seven_code_16_trans_2_g));  // open: dp
  Multiplexer #(.width(4)) multiplexer_4 (
    .in0({multiplexer_3_out[3], subtractor_4bit_1_d[2:0]}), .in1({A[3], adder_4bit_1_s[2:0]}), .out(Y0),
    .sel(or_1_out));
  or or_3 (Y1, adder_4bit_1_s[3], subtractor_4bit_1_d[3]);
  seven_code_16_trans seven_code_16_trans_3 (
    .m0(Y0[0]), .m1(Y0[1]), .m2(Y0[2]), .a(seven_code_16_trans_3_a), .b(seven_code_16_trans_3_b),
    .c(seven_code_16_trans_3_c), .d(seven_code_16_trans_3_d), .e(seven_code_16_trans_3_e),
    .f(seven_code_16_trans_3_f), .g(seven_code_16_trans_3_g));  // open: m3, h
  _7_Segment_Display u_7_segment_display_5 (.g(Y0[3]));  // open: f, a, b, e, d, c, dp
  _7_Segment_Display u_7_segment_display_6 (
    .g(seven_code_16_trans_3_a), .f(seven_code_16_trans_3_b), .a(seven_code_16_trans_3_c),
    .b(seven_code_16_trans_3_d), .e(seven_code_16_trans_3_e), .d(seven_code_16_trans_3_f),
    .c(seven_code_16_trans_3_g));  // open: dp

  // Notes on the sheet:
  //   A如果比B大
  //   B符号
  //   A符号
  //   A
  //   B
endmodule

module OnesComplementAdder (
  input  [3:0] A,
  input  [3:0] B,
  output [3:0] Y0,
  output Y1
);

  wire seven_code_16_trans_1_a, seven_code_16_trans_1_b, seven_code_16_trans_1_c, seven_code_16_trans_1_d,
       seven_code_16_trans_1_e, seven_code_16_trans_1_f, seven_code_16_trans_1_g;
  wire [3:0] signmagnitude_to_onescomplement_converter_1_out_2,
       signmagnitude_to_onescomplement_converter_2_out_2;

  SignMagnitude_To_OnesComplement_Converter signmagnitude_to_onescomplement_converter_1 (
    .in_1(A), .out_2(signmagnitude_to_onescomplement_converter_1_out_2));
  SignMagnitude_To_OnesComplement_Converter signmagnitude_to_onescomplement_converter_2 (
    .in_1(B), .out_2(signmagnitude_to_onescomplement_converter_2_out_2));
  SMA_4bit_2 sma_4bit_2_1 (
    .A(signmagnitude_to_onescomplement_converter_1_out_2),
    .B(signmagnitude_to_onescomplement_converter_2_out_2), .Y0(Y0), .Y1(Y1));
  seven_code_16_trans seven_code_16_trans_1 (
    .m0(Y0[0]), .m1(Y0[1]), .m2(Y0[2]), .m3(Y1), .a(seven_code_16_trans_1_a), .b(seven_code_16_trans_1_b),
    .c(seven_code_16_trans_1_c), .d(seven_code_16_trans_1_d), .e(seven_code_16_trans_1_e),
    .f(seven_code_16_trans_1_f), .g(seven_code_16_trans_1_g));  // open: h
  _7_Segment_Display u_7_segment_display_1 (.g(Y0[3]));  // open: f, a, b, e, d, c, dp
  _7_Segment_Display u_7_segment_display_2 (
    .g(seven_code_16_trans_1_a), .f(seven_code_16_trans_1_b), .a(seven_code_16_trans_1_c),
    .b(seven_code_16_trans_1_d), .e(seven_code_16_trans_1_e), .d(seven_code_16_trans_1_f),
    .c(seven_code_16_trans_1_g));  // open: dp
endmodule

module SignMagnitude_To_OnesComplement_Converter (
  input  [3:0] in_1,
  output [3:0] out_2
);

  xor xor_1 (out_2[2], in_1[2], in_1[3]);
  xor xor_2 (out_2[1], in_1[1], in_1[3]);
  xor xor_3 (out_2[0], in_1[0], in_1[3]);

  assign out_2[3] = in_1[3];
endmodule

module SMA_4bit_2 (
  input  [3:0] A,
  input  [3:0] B,
  output [3:0] Y0,
  output Y1
);

  wire and_1_out, and_2_out, and_3_out, and_4_out, and_5_out, nor_1_out, or_1_out, or_2_out, or_3_out,
       seven_code_16_trans_1_a, seven_code_16_trans_1_b, seven_code_16_trans_1_c, seven_code_16_trans_1_d,
       seven_code_16_trans_1_e, seven_code_16_trans_1_f, seven_code_16_trans_1_g, seven_code_16_trans_2_a,
       seven_code_16_trans_2_b, seven_code_16_trans_2_c, seven_code_16_trans_2_d, seven_code_16_trans_2_e,
       seven_code_16_trans_2_f, seven_code_16_trans_2_g, seven_code_16_trans_3_a, seven_code_16_trans_3_b,
       seven_code_16_trans_3_c, seven_code_16_trans_3_d, seven_code_16_trans_3_e, seven_code_16_trans_3_f,
       seven_code_16_trans_3_g, xor_1_out, xor_2_out, xor_3_out;
  wire [3:0] adder_4bit_1_s, multiplexer_1_out, multiplexer_2_out, subtractor_4bit_1_d;
  wire [3:3] multiplexer_3_out;

  and and_1 (and_1_out, ~A[3], ~B[3]);  // AND_Gate
  and and_2 (and_2_out, A[3], B[3]);
  or or_1 (or_1_out, and_2_out, and_1_out);
  nor nor_1 (nor_1_out, A[0], B[0], A[1], B[1], A[2], B[2]);
  and and_3 (and_3_out, A[2], ~B[2]);  // AND_Gate
  xor xor_1 (xor_1_out, A[2], B[2]);
  xor xor_2 (xor_2_out, A[2], B[2]);
  and and_4 (and_4_out, ~xor_1_out, A[1], ~B[1]);  // AND_Gate
  xor xor_3 (xor_3_out, A[1], B[1]);
  and and_5 (and_5_out, ~xor_2_out, ~xor_3_out, ~A[0], B[0]);  // AND_Gate
  Multiplexer #(.width(4)) multiplexer_1 (.in0(B), .in1(A), .out(multiplexer_1_out), .sel(or_2_out));
  or or_2 (or_2_out, and_3_out, and_4_out, and_5_out);
  Multiplexer #(.width(4)) multiplexer_2 (.in0(A), .in1(B), .out(multiplexer_2_out), .sel(or_2_out));
  adder_4bit adder_4bit_1 (.A(A), .B(B), .S(adder_4bit_1_s));  // open: Cin, Cout
  seven_code_16_trans seven_code_16_trans_1 (
    .m0(A[0]), .m1(A[1]), .m2(A[2]), .a(seven_code_16_trans_1_a), .b(seven_code_16_trans_1_b),
    .c(seven_code_16_trans_1_c), .d(seven_code_16_trans_1_d), .e(seven_code_16_trans_1_e),
    .f(seven_code_16_trans_1_f), .g(seven_code_16_trans_1_g));  // open: m3, h
  seven_code_16_trans seven_code_16_trans_2 (
    .m0(B[0]), .m1(B[1]), .m2(B[2]), .a(seven_code_16_trans_2_a), .b(seven_code_16_trans_2_b),
    .c(seven_code_16_trans_2_c), .d(seven_code_16_trans_2_d), .e(seven_code_16_trans_2_e),
    .f(seven_code_16_trans_2_f), .g(seven_code_16_trans_2_g));  // open: m3, h
  Multiplexer multiplexer_3 (.in0(B[3]), .in1(A[3]), .out(multiplexer_3_out[3]), .sel(or_2_out));
  subtractor_4bit subtractor_4bit_1 (
    .A(multiplexer_1_out), .B(multiplexer_2_out), .D(subtractor_4bit_1_d));  // open: Bin, Bout
  _7_Segment_Display u_7_segment_display_1 (.g(A[3]));  // open: f, a, b, e, d, c, dp
  _7_Segment_Display u_7_segment_display_2 (
    .g(seven_code_16_trans_1_a), .f(seven_code_16_trans_1_b), .a(seven_code_16_trans_1_c),
    .b(seven_code_16_trans_1_d), .e(seven_code_16_trans_1_e), .d(seven_code_16_trans_1_f),
    .c(seven_code_16_trans_1_g));  // open: dp
  _7_Segment_Display u_7_segment_display_3 (.g(B[3]));  // open: f, a, b, e, d, c, dp
  _7_Segment_Display u_7_segment_display_4 (
    .g(seven_code_16_trans_2_a), .f(seven_code_16_trans_2_b), .a(seven_code_16_trans_2_c),
    .b(seven_code_16_trans_2_d), .e(seven_code_16_trans_2_e), .d(seven_code_16_trans_2_f),
    .c(seven_code_16_trans_2_g));  // open: dp
  and and_6 (Y1, ~nor_1_out, or_3_out);  // AND_Gate
  Multiplexer #(.width(4)) multiplexer_4 (
    .in0({multiplexer_3_out[3], subtractor_4bit_1_d[2:0]}), .in1({A[3], adder_4bit_1_s[2:0]}), .out(Y0),
    .sel(or_1_out));
  or or_3 (or_3_out, adder_4bit_1_s[3], subtractor_4bit_1_d[3]);
  seven_code_16_trans seven_code_16_trans_3 (
    .m0(Y0[0]), .m1(Y0[1]), .m2(Y0[2]), .m3(Y1), .a(seven_code_16_trans_3_a), .b(seven_code_16_trans_3_b),
    .c(seven_code_16_trans_3_c), .d(seven_code_16_trans_3_d), .e(seven_code_16_trans_3_e),
    .f(seven_code_16_trans_3_f), .g(seven_code_16_trans_3_g));  // open: h
  _7_Segment_Display u_7_segment_display_5 (.g(Y0[3]));  // open: f, a, b, e, d, c, dp
  _7_Segment_Display u_7_segment_display_6 (
    .g(seven_code_16_trans_3_a), .f(seven_code_16_trans_3_b), .a(seven_code_16_trans_3_c),
    .b(seven_code_16_trans_3_d), .e(seven_code_16_trans_3_e), .d(seven_code_16_trans_3_f),
    .c(seven_code_16_trans_3_g));  // open: dp

  // Notes on the sheet:
  //   A如果比B大
  //   B符号
  //   A符号
  //   A
  //   B
endmodule

module OnesComplementAdder_1 (
  input  [3:0] A,
  input  [3:0] B,
  output [3:0] S
);

  wire and_1_out, and_2_out, xor_1_out;
  wire [0:0] or_1_out;
  wire [3:0] adder_4bit_1_s;

  xor xor_1 (xor_1_out, A[3], B[3]);
  and and_1 (and_1_out, A[3], B[3]);
  and and_2 (and_2_out, ~adder_4bit_1_s[3], xor_1_out);  // AND_Gate
  adder_4bit adder_4bit_1 (.A(A), .B(B), .S(adder_4bit_1_s));  // open: Cin, Cout
  or or_1 (or_1_out[0], and_1_out, and_2_out);
  adder_4bit adder_4bit_2 (.A(adder_4bit_1_s), .B({3'b000, or_1_out[0]}), .S(S));  // open: Cin, Cout

  // Notes on the sheet:
  //   不加1
endmodule

module OnesComplementAdder_2 (
  input  [3:0] A,
  input  [3:0] B,
  output [3:0] S
);

  wire [0:0] adder_4bit_1_cout;
  wire [3:0] adder_4bit_1_s;

  adder_4bit adder_4bit_1 (.A(A), .B(B), .S(adder_4bit_1_s), .Cout(adder_4bit_1_cout[0]));  // open: Cin
  adder_4bit adder_4bit_2 (.A(adder_4bit_1_s), .B({3'b000, adder_4bit_1_cout[0]}), .S(S));  // open: Cin, Cout

  // Notes on the sheet:
  //   不加1
endmodule

module adder_4bit_overflow (
  input  Cin,
  input  [3:0] A,
  input  [3:0] B,
  output [3:0] S,
  output Cout,
  output f
);

  wire and_2_out, and_3_out, and_4_out, and_5_out, not_1_out, or_1_out, or_2_out, xor_1_out;
  wire [3:0] adder_4bit_2_s;

  adder_4bit adder_4bit_1 (.A(A), .B(B), .Cin(Cin), .S(S), .Cout(Cout));
  xor xor_1 (xor_1_out, A[3], B[3]);
  not not_1 (not_1_out, xor_1_out);
  adder_4bit adder_4bit_2 (.A({1'b0, A[2:0]}), .B({1'b0, B[2:0]}), .Cin(Cin), .S(adder_4bit_2_s));  // open: Cout
  or or_1 (or_1_out, and_2_out, and_3_out);
  or or_2 (or_2_out, adder_4bit_2_s[3], or_1_out);
  and and_1 (f, or_2_out, not_1_out);
  and and_2 (and_2_out, and_5_out, ~Cin);  // AND_Gate
  buf and_3 (and_3_out, and_4_out);  // AND_Gate
  and and_4 (and_4_out, adder_4bit_2_s[0], adder_4bit_2_s[1], adder_4bit_2_s[2]);
  and and_5 (and_5_out, ~adder_4bit_2_s[2], ~adder_4bit_2_s[1], ~adder_4bit_2_s[0]);  // AND_Gate
endmodule

module adder_4bit_overflow_true (
  input  Cin,
  input  [3:0] A,
  input  [3:0] B,
  output [3:0] S,
  output Cout,
  output f
);

  wire [3:0] adder_4bit_2_s;

  adder_4bit adder_4bit_1 (.A(A), .B(B), .Cin(Cin), .S(S), .Cout(Cout));
  adder_4bit adder_4bit_2 (.A({1'b0, A[2:0]}), .B({1'b0, B[2:0]}), .Cin(Cin), .S(adder_4bit_2_s));  // open: Cout
  xor xor_1 (f, adder_4bit_2_s[3], Cout);
endmodule

module SR_Latch (
  input  A,
  input  B,
  output Q,
  output Qn
);

  nor nor_1 (Q, A, Qn);
  nor nor_2 (Qn, Q, B);
endmodule

module SR_Latch_1 (
  input  S1,
  input  R1,
  output Qn,
  output Q
);

  wire and_1_out, and_2_out, dipswitch_1_sw1, dipswitch_1_sw2, or_1_out, or_2_out;

  DipSwitch dipswitch_1 (.sw1(dipswitch_1_sw1), .sw2(dipswitch_1_sw2));  // open: sw3, sw4, sw5, sw6, sw7, sw8
  and and_1 (and_1_out, S1, dipswitch_1_sw2);
  and and_2 (and_2_out, dipswitch_1_sw2, R1);
  or or_1 (or_1_out, dipswitch_1_sw1, and_1_out);
  or or_2 (or_2_out, and_2_out, dipswitch_1_sw1);
  nand nand_1 (Qn, or_1_out, Q);
  nand nand_2 (Q, Qn, or_2_out);
endmodule

module D_Latch (
  input  WE,
  input  D,
  input  Z,
  output Qn,
  output Q
);

  wire and_1_out, and_2_out, multiplexer_1_out, multiplexer_2_out, not_1_out;

  not not_1 (not_1_out, D);
  Multiplexer multiplexer_1 (.in0(and_1_out), .in1(1'b0), .out(multiplexer_1_out), .sel(Z));
  and and_1 (and_1_out, D, WE);
  and and_2 (and_2_out, WE, not_1_out);
  Multiplexer multiplexer_2 (.in0(and_2_out), .in1(1'b1), .out(multiplexer_2_out), .sel(Z));
  SR_Latch sr_latch_1 (.A(multiplexer_1_out), .B(multiplexer_2_out), .Q(Qn), .Qn(Q));
endmodule

module DFF (
  input  CLK,
  input  D,
  input  Z,
  output Qn,
  output Q
);

  wire d_latch_1_q, not_1_out;

  not not_1 (not_1_out, CLK);
  D_Latch d_latch_1 (.WE(not_1_out), .D(D), .Z(Z), .Q(d_latch_1_q));  // open: Qn
  D_Latch d_latch_2 (.WE(CLK), .D(d_latch_1_q), .Z(Z), .Qn(Qn), .Q(Q));
endmodule

module DFF_1 (
  input  Z,
  input  CLK,
  input  D,
  output Qn,
  output Q
);

  wire dff_1_q, dff_1_qn, not_1_out;

  not not_1 (not_1_out, Z);
  DFF dff_1 (.CLK(CLK), .D(D), .Qn(dff_1_qn), .Q(dff_1_q));  // open: Z
  and and_1 (Qn, not_1_out, dff_1_qn);
  and and_2 (Q, dff_1_q, not_1_out);
endmodule

module DFF_2 (
  output out_1,
  output out_2
);

  wire button_1_out;

  Button button_1 (.out(button_1_out));
  DFF_1 dff_1_1 (.CLK(button_1_out), .D(out_1), .Qn(out_1), .Q(out_2));  // open: Z
endmodule

module DFF_reverse (
  input  Z,
  input  CLK_re,
  input  D,
  output Qn,
  output Q
);

  wire not_1_out;

  not not_1 (not_1_out, CLK_re);
  DFF_1 dff_1_1 (.Z(Z), .CLK(not_1_out), .D(D), .Qn(Qn), .Q(Q));
endmodule

module DFF_3 (
  input  Z,
  input  CLK,
  input  D,
  input  EN,
  output Qn,
  output Q
);

  wire multiplexer_1_out;

  Multiplexer multiplexer_1 (.in0(Q), .in1(D), .out(multiplexer_1_out), .sel(EN));
  DFF_1 dff_1_1 (.Z(Z), .CLK(CLK), .D(multiplexer_1_out), .Qn(Qn), .Q(Q));
endmodule

module Register_4bit (
  input  [3:0] D,
  input  EN,
  input  Z,
  input  CLK,
  output [3:0] Y
);

  wire seven_code_16_trans_1_a, seven_code_16_trans_1_b, seven_code_16_trans_1_c, seven_code_16_trans_1_d,
       seven_code_16_trans_1_e, seven_code_16_trans_1_f, seven_code_16_trans_1_g;

  DFF_3 dff_3_1 (.Z(Z), .CLK(CLK), .D(D[0]), .EN(EN), .Q(Y[0]));  // open: Qn
  DFF_3 dff_3_2 (.Z(Z), .CLK(CLK), .D(D[1]), .EN(EN), .Q(Y[1]));  // open: Qn
  DFF_3 dff_3_3 (.Z(Z), .CLK(CLK), .D(D[2]), .EN(EN), .Q(Y[2]));  // open: Qn
  DFF_3 dff_3_4 (.Z(Z), .CLK(CLK), .D(D[3]), .EN(EN), .Q(Y[3]));  // open: Qn
  seven_code_16_trans seven_code_16_trans_1 (
    .m0(Y[0]), .m1(Y[1]), .m2(Y[2]), .m3(Y[3]), .a(seven_code_16_trans_1_a), .b(seven_code_16_trans_1_b),
    .c(seven_code_16_trans_1_c), .d(seven_code_16_trans_1_d), .e(seven_code_16_trans_1_e),
    .f(seven_code_16_trans_1_f), .g(seven_code_16_trans_1_g));  // open: h
  _7_Segment_Display u_7_segment_display_1 (
    .g(seven_code_16_trans_1_a), .f(seven_code_16_trans_1_b), .a(seven_code_16_trans_1_c),
    .b(seven_code_16_trans_1_d), .e(seven_code_16_trans_1_e), .d(seven_code_16_trans_1_f),
    .c(seven_code_16_trans_1_g));  // open: dp
endmodule

module Counter_4bit (
  input  EN,
  output [3:0] out_2
);

  wire button_1_out;
  wire [3:0] register_4bit_1_y;

  Button button_1 (.out(button_1_out));
  Register_4bit register_4bit_1 (.D(out_2), .EN(EN), .CLK(button_1_out), .Y(register_4bit_1_y));  // open: Z
  adder_4bit_overflow_true adder_4bit_overflow_true_1 (
    .A(register_4bit_1_y), .B(4'b0001), .S(out_2));  // open: Cin, Cout, f
endmodule

module Register_8bit (
  input  [7:0] D,
  input  EN,
  input  Z,
  input  CLK,
  output [7:0] Y
);

  Register_4bit register_4bit_1 (.D(D[3:0]), .EN(EN), .Z(Z), .CLK(CLK), .Y(Y[3:0]));
  Register_4bit register_4bit_2 (.D(D[7:4]), .EN(EN), .Z(Z), .CLK(CLK), .Y(Y[7:4]));
endmodule

module adder_8bit (
  input  [7:0] A,
  input  [7:0] B,
  input  Cin,
  output [7:0] S,
  output Cout
);

  wire adder_4bit_1_cout;

  adder_4bit adder_4bit_1 (.A(A[3:0]), .B(B[3:0]), .Cin(Cin), .S(S[3:0]), .Cout(adder_4bit_1_cout));
  adder_4bit adder_4bit_2 (.A(A[7:4]), .B(B[7:4]), .Cin(adder_4bit_1_cout), .S(S[7:4]), .Cout(Cout));
endmodule

module Counter_8bit (
  input  EN,
  input  Z,
  input  CLK,
  input  CLR,
  output [7:0] Y
);

  wire [7:0] adder_8bit_1_s, multiplexer_1_out;

  Multiplexer #(.select(2), .width(8)) multiplexer_1 (
    .in0(Y), .in1(adder_8bit_1_s), .in2({8{1'b0}}), .in3({8{1'b0}}), .out(multiplexer_1_out), .sel({CLR, EN}));
  Register_8bit register_8bit_1 (.D(multiplexer_1_out), .EN(1'b1), .Z(Z), .CLK(CLK), .Y(Y));
  adder_8bit adder_8bit_1 (.A(Y), .B(8'h1), .S(adder_8bit_1_s));  // open: Cin, Cout
endmodule

module Sequence_1to10 (
  input  Z,
  input  EN,
  output [7:0] out_3,
  output [7:0] Y
);

  wire CLK_out;
  wire [7:0] adder_8bit_1_s;

  Clock CLK (.out(CLK_out));
  Counter_8bit counter_8bit_1 (.EN(EN), .Z(Z), .CLK(CLK_out), .Y(out_3));  // open: CLR
  adder_8bit adder_8bit_1 (.A(out_3), .B(Y), .S(adder_8bit_1_s));  // open: Cin, Cout
  Register_8bit register_8bit_1 (.D(adder_8bit_1_s), .EN(EN), .Z(Z), .CLK(CLK_out), .Y(Y));
endmodule

module Clock_digital (
  input  EN,
  input  Z,
  input  CLR
);

  wire and_1_out, CLK_out, or_1_out, seven_code_trans_1_a, seven_code_trans_1_b, seven_code_trans_1_c,
       seven_code_trans_1_d, seven_code_trans_1_e, seven_code_trans_1_f, seven_code_trans_1_g,
       seven_code_trans_1_h, seven_code_trans_2_a, seven_code_trans_2_b, seven_code_trans_2_c,
       seven_code_trans_2_d, seven_code_trans_2_e, seven_code_trans_2_f, seven_code_trans_2_g,
       seven_code_trans_2_h, seven_code_trans_3_a, seven_code_trans_3_b, seven_code_trans_3_c,
       seven_code_trans_3_d, seven_code_trans_3_e, seven_code_trans_3_f, seven_code_trans_3_g,
       seven_code_trans_3_h, seven_code_trans_4_a, seven_code_trans_4_b, seven_code_trans_4_c,
       seven_code_trans_4_d, seven_code_trans_4_e, seven_code_trans_4_f, seven_code_trans_4_g,
       seven_code_trans_4_h;
  wire [3:0] binary_to_bcd_converter_1_p2, binary_to_bcd_converter_1_p3, binary_to_bcd_converter_2_p2,
       binary_to_bcd_converter_2_p3;
  wire [7:0] counter_8bit_1_y, counter_8bit_2_y;

  or or_1 (or_1_out, and_1_out, CLR);
  Clock CLK (.out(CLK_out));
  and and_1 (and_1_out, binary_to_bcd_converter_1_p2[2], binary_to_bcd_converter_1_p2[0], binary_to_bcd_converter_1_p3[0], binary_to_bcd_converter_1_p3[3]);
  Counter_8bit counter_8bit_1 (.EN(EN), .Z(Z), .CLK(CLK_out), .CLR(or_1_out), .Y(counter_8bit_1_y));
  Counter_8bit counter_8bit_2 (.EN(and_1_out), .Z(Z), .CLK(CLK_out), .CLR(CLR), .Y(counter_8bit_2_y));
  // Binary_to_BCD_converter #(.binvalue(8)) binary_to_bcd_converter_1: pin names not known; wires that end beside it: counter_8bit_1_y, binary_to_bcd_converter_1_p2, binary_to_bcd_converter_1_p3
  // Binary_to_BCD_converter #(.binvalue(8)) binary_to_bcd_converter_2: pin names not known; wires that end beside it: counter_8bit_2_y, binary_to_bcd_converter_2_p2, binary_to_bcd_converter_2_p3
  seven_code_trans seven_code_trans_1 (
    .m0(binary_to_bcd_converter_1_p2[0]), .m1(binary_to_bcd_converter_1_p2[1]),
    .m2(binary_to_bcd_converter_1_p2[2]), .m3(binary_to_bcd_converter_1_p2[3]), .a(seven_code_trans_1_a),
    .b(seven_code_trans_1_b), .c(seven_code_trans_1_c), .d(seven_code_trans_1_d), .e(seven_code_trans_1_e),
    .f(seven_code_trans_1_f), .g(seven_code_trans_1_g), .h(seven_code_trans_1_h));
  seven_code_trans seven_code_trans_2 (
    .m0(binary_to_bcd_converter_1_p3[0]), .m1(binary_to_bcd_converter_1_p3[1]),
    .m2(binary_to_bcd_converter_1_p3[2]), .m3(binary_to_bcd_converter_1_p3[3]), .a(seven_code_trans_2_a),
    .b(seven_code_trans_2_b), .c(seven_code_trans_2_c), .d(seven_code_trans_2_d), .e(seven_code_trans_2_e),
    .f(seven_code_trans_2_f), .g(seven_code_trans_2_g), .h(seven_code_trans_2_h));
  seven_code_trans seven_code_trans_3 (
    .m0(binary_to_bcd_converter_2_p2[0]), .m1(binary_to_bcd_converter_2_p2[1]),
    .m2(binary_to_bcd_converter_2_p2[2]), .m3(binary_to_bcd_converter_2_p2[3]), .a(seven_code_trans_3_a),
    .b(seven_code_trans_3_b), .c(seven_code_trans_3_c), .d(seven_code_trans_3_d), .e(seven_code_trans_3_e),
    .f(seven_code_trans_3_f), .g(seven_code_trans_3_g), .h(seven_code_trans_3_h));
  seven_code_trans seven_code_trans_4 (
    .m0(binary_to_bcd_converter_2_p3[0]), .m1(binary_to_bcd_converter_2_p3[1]),
    .m2(binary_to_bcd_converter_2_p3[2]), .m3(binary_to_bcd_converter_2_p3[3]), .a(seven_code_trans_4_a),
    .b(seven_code_trans_4_b), .c(seven_code_trans_4_c), .d(seven_code_trans_4_d), .e(seven_code_trans_4_e),
    .f(seven_code_trans_4_f), .g(seven_code_trans_4_g), .h(seven_code_trans_4_h));
  _7_Segment_Display u_7_segment_display_1 (
    .g(seven_code_trans_3_a), .f(seven_code_trans_3_b), .a(seven_code_trans_3_c), .b(seven_code_trans_3_d),
    .e(seven_code_trans_3_e), .d(seven_code_trans_3_f), .c(seven_code_trans_3_g), .dp(seven_code_trans_3_h));
  _7_Segment_Display u_7_segment_display_2 (
    .g(seven_code_trans_1_a), .f(seven_code_trans_1_b), .a(seven_code_trans_1_c), .b(seven_code_trans_1_d),
    .e(seven_code_trans_1_e), .d(seven_code_trans_1_f), .c(seven_code_trans_1_g), .dp(seven_code_trans_1_h));
  _7_Segment_Display u_7_segment_display_3 (
    .g(seven_code_trans_4_a), .f(seven_code_trans_4_b), .a(seven_code_trans_4_c), .b(seven_code_trans_4_d),
    .e(seven_code_trans_4_e), .d(seven_code_trans_4_f), .c(seven_code_trans_4_g), .dp(seven_code_trans_4_h));
  _7_Segment_Display u_7_segment_display_4 (
    .g(seven_code_trans_2_a), .f(seven_code_trans_2_b), .a(seven_code_trans_2_c), .b(seven_code_trans_2_d),
    .e(seven_code_trans_2_e), .d(seven_code_trans_2_f), .c(seven_code_trans_2_g), .dp(seven_code_trans_2_h));

  // Notes on the sheet:
  //   2
  //   2
  //   1
  //   1
  //   分
  //   秒
endmodule

module ROM_16MUL8 (
  input  [3:0] PC_in,
  output [7:0] inst
);

  Multiplexer #(.select(4), .width(8)) multiplexer_1 (
    .in0(8'h86), .in1(8'h92), .in2(8'h1), .in3(8'h90), .in4(8'ha0), .in5(8'hb1), .in6(8'h17), .in7(8'h29),
    .in8(8'hf9), .in9(8'hc3), .out(inst), .sel(PC_in));  // open: in10, in11, in12, in13, in14, in15
endmodule

module RAM_8MUL8 (
  input  EN,
  input  [7:0] wdata,
  input  [2:0] waddr,
  input  CLK,
  input  CLR,
  output [7:0] rdata
);

  wire decoder_1_out0, decoder_1_out1, decoder_1_out2, decoder_1_out3, decoder_1_out4, decoder_1_out5,
       decoder_1_out6, decoder_1_out7;
  wire [7:0] register_1_q, register_2_q, register_3_q, register_4_q, register_5_q, register_6_q,
       register_7_q, register_8_q;

  Decoder #(.select(3)) decoder_1 (
    .out0(decoder_1_out0), .out1(decoder_1_out1), .out2(decoder_1_out2), .out3(decoder_1_out3),
    .out4(decoder_1_out4), .out5(decoder_1_out5), .out6(decoder_1_out6), .out7(decoder_1_out7), .sel(waddr),
    .en(EN));
  Register register_1 (.D(wdata), .en(decoder_1_out0), .clk(CLK), .Q(register_1_q), .clr(CLR));
  Register register_2 (.D(wdata), .en(decoder_1_out1), .clk(CLK), .Q(register_2_q), .clr(CLR));
  Register register_3 (.D(wdata), .en(decoder_1_out2), .clk(CLK), .Q(register_3_q), .clr(CLR));
  Register register_4 (.D(wdata), .en(decoder_1_out3), .clk(CLK), .Q(register_4_q), .clr(CLR));
  Register register_5 (.D(wdata), .en(decoder_1_out4), .clk(CLK), .Q(register_5_q), .clr(CLR));
  Register register_6 (.D(wdata), .en(decoder_1_out5), .clk(CLK), .Q(register_6_q), .clr(CLR));
  Register register_7 (.D(wdata), .en(decoder_1_out6), .clk(CLK), .Q(register_7_q), .clr(CLR));
  Register register_8 (.D(wdata), .en(decoder_1_out7), .clk(CLK), .Q(register_8_q), .clr(CLR));
  Multiplexer #(.select(3), .width(8)) multiplexer_1 (
    .in0(register_1_q), .in1(register_2_q), .in2(register_3_q), .in3(register_4_q), .in4(register_5_q),
    .in5(register_6_q), .in6(register_7_q), .in7(register_8_q), .out(rdata), .sel(waddr));
endmodule

module sCPU_li_add (
  input  EN,
  input  CLR,
  output [7:0] rdata2,
  output [7:0] rdata1
);

  wire and_1_out, and_2_out, and_3_out, and_11_out, and_12_out, and_13_out, CLK_out, comparator_1_gt,
       comparator_1_lt, decoder_1_out0, decoder_1_out1, decoder_1_out2, decoder_1_out3, decoder_2_out0,
       decoder_2_out1, decoder_2_out2, decoder_2_out3, decoder_2_out4, decoder_2_out5, decoder_2_out6,
       decoder_2_out7, decoder_3_out0, decoder_3_out1, multiplexer_2_out, not_1_out, not_2_out, or_1_out,
       or_5_out;
  wire [2:0] and_7_out, and_8_out, and_9_out, and_10_out, bit_extender_4_out, bit_extender_5_out,
       bit_extender_6_out, or_4_out, or_6_out;
  wire [3:0] adder_1_out, pc_1_pc_out;
  wire [7:0] adder_2_out, and_4_out, and_5_out, and_6_out, bit_extender_1_out, bit_extender_2_out,
       bit_extender_3_out, button_1_out, demultiplexer_1_out0, demultiplexer_1_out1, dipswitch_1_sw1,
       multiplexer_1_out, multiplexer_3_out, multiplexer_4_out, or_2_out, or_3_out, register_1_q,
       register_2_q, register_3_q, register_4_q, register_5_q, register_6_q, register_7_q, register_8_q,
       register_9_q, register_10_q;

  DipSwitch dipswitch_1 (
    .sw1(dipswitch_1_sw1[0]), .sw2(dipswitch_1_sw1[1]), .sw3(dipswitch_1_sw1[2]), .sw4(dipswitch_1_sw1[3]),
    .sw5(dipswitch_1_sw1[4]), .sw6(dipswitch_1_sw1[5]), .sw7(dipswitch_1_sw1[6]), .sw8(dipswitch_1_sw1[7]));
  Button button_1 (.out(button_1_out[0]));
  Button button_2 (.out(button_1_out[1]));
  Button button_3 (.out(button_1_out[2]));
  Button button_4 (.out(button_1_out[3]));
  Button button_5 (.out(button_1_out[4]));
  Button button_6 (.out(button_1_out[5]));
  Button button_7 (.out(button_1_out[6]));
  Button button_8 (.out(button_1_out[7]));
  Multiplexer #(.select(3), .width(8)) multiplexer_1 (
    .in0(dipswitch_1_sw1), .in1(button_1_out), .in2({8{1'b0}}), .in3({8{1'b0}}), .in4({8{1'b0}}),
    .in5({8{1'b0}}), .in6({8{1'b0}}), .in7({8{1'b0}}), .out(multiplexer_1_out), .sel(multiplexer_3_out[2:0]));
  Clock CLK (.out(CLK_out));
  and and_1 (and_1_out, or_5_out, decoder_1_out3);
  Multiplexer multiplexer_2 (.in0(1'b0), .in1(1'b1), .out(multiplexer_2_out), .sel(and_1_out));
  Multiplexer #(.select(4), .width(8)) multiplexer_3 (
    .in0(8'h86), .in1(8'h92), .in2(8'h1), .in3(8'h91), .in4(8'ha0), .in5(8'hb0), .in6(8'h29), .in7(8'h68),
    .in8(8'h3e), .in9(8'hf6), .in10(8'h80), .in11(8'h61), .in12(8'hca), .in13(8'hf9), .in14(8'h79),
    .in15(8'hc1), .out(multiplexer_3_out), .sel(pc_1_pc_out));
  PC pc_1 (.datain(adder_1_out), .ctr(multiplexer_2_out), .CLK(CLK_out), .CLR(CLR), .PC_out(pc_1_pc_out));
  Adder #(.width(4)) adder_1 (.a(multiplexer_3_out[5:2]), .b(pc_1_pc_out), .out(adder_1_out));  // open: cin, cout
  not not_1 (not_1_out, multiplexer_3_out[3]);
  not not_2 (not_2_out, multiplexer_3_out[3]);
  and and_2 (and_2_out, decoder_1_out1, not_1_out);
  Decoder #(.select(2)) decoder_1 (
    .out0(decoder_1_out0), .out1(decoder_1_out1), .out2(decoder_1_out2), .out3(decoder_1_out3),
    .sel(multiplexer_3_out[7:6]), .en(1'b1));
  Multiplexer #(.select(2), .width(8)) multiplexer_4 (
    .in0({{6{1'b0}}, multiplexer_3_out[1:0]}), .in1({4'b0000, multiplexer_3_out[1:0], 2'b00}),
    .in2({2'b00, multiplexer_3_out[1:0], 4'b0000}), .in3({multiplexer_3_out[1:0], {6{1'b0}}}),
    .out(multiplexer_4_out), .sel(multiplexer_3_out[3:2]));
  assign bit_extender_1_out = {{7{not_2_out}}, not_2_out};  // Bit_Extender bit_extender_1
  assign bit_extender_2_out = {{7{decoder_1_out0}}, decoder_1_out0};  // Bit_Extender bit_extender_2
  assign bit_extender_3_out = {{7{decoder_1_out2}}, decoder_1_out2};  // Bit_Extender bit_extender_3
  or or_1 (or_1_out, decoder_1_out2, and_2_out, decoder_1_out0);
  assign bit_extender_4_out = {{2{decoder_1_out0}}, decoder_1_out0};  // Bit_Extender bit_extender_4
  assign bit_extender_5_out = {{2{decoder_1_out3}}, decoder_1_out3};  // Bit_Extender bit_extender_5
  Decoder #(.select(3)) decoder_2 (
    .out0(decoder_2_out0), .out1(decoder_2_out1), .out2(decoder_2_out2), .out3(decoder_2_out3),
    .out4(decoder_2_out4), .out5(decoder_2_out5), .out6(decoder_2_out6), .out7(decoder_2_out7),
    .sel({1'b0, multiplexer_3_out[5:4]}), .en(and_3_out));
  and and_3 (and_3_out, EN, or_1_out);
  assign and_4_out = bit_extender_1_out & multiplexer_1_out;  // AND_Gate and_4, 8 bits wide
  assign and_5_out = bit_extender_3_out & multiplexer_4_out;  // AND_Gate and_5, 8 bits wide
  assign and_6_out = bit_extender_2_out & adder_2_out;  // AND_Gate and_6, 8 bits wide
  assign and_7_out = {1'b0, multiplexer_3_out[1:0]} & bit_extender_4_out;  // AND_Gate and_7, 3 bits wide
  assign and_8_out = {1'b0, multiplexer_3_out[3:2]} & bit_extender_4_out;  // AND_Gate and_8, 3 bits wide
  assign and_9_out = {1'b0, multiplexer_3_out[1:0]} & bit_extender_5_out;  // AND_Gate and_9, 3 bits wide
  assign or_2_out = and_4_out | or_3_out;  // OR_Gate or_2, 8 bits wide
  assign or_3_out = and_5_out | and_6_out;  // OR_Gate or_3, 8 bits wide
  assign bit_extender_6_out = {{2{decoder_1_out1}}, decoder_1_out1};  // Bit_Extender bit_extender_6
  assign and_10_out = {1'b0, multiplexer_3_out[5:4]} & bit_extender_6_out;  // AND_Gate and_10, 3 bits wide
  Register register_1 (.D(or_2_out), .en(decoder_2_out0), .clk(CLK_out), .Q(register_1_q), .clr(CLR));
  Register register_2 (.D(or_2_out), .en(decoder_2_out1), .clk(CLK_out), .Q(register_2_q), .clr(CLR));
  Register register_3 (.D(or_2_out), .en(decoder_2_out2), .clk(CLK_out), .Q(register_3_q), .clr(CLR));
  Register register_4 (.D(or_2_out), .en(decoder_2_out3), .clk(CLK_out), .Q(register_4_q), .clr(CLR));
  assign or_4_out = and_10_out | and_8_out;  // OR_Gate or_4, 3 bits wide
  or or_5 (or_5_out, comparator_1_gt, comparator_1_lt);
  Register register_5 (.D(or_2_out), .en(decoder_2_out4), .clk(CLK_out), .Q(register_5_q), .clr(CLR));
  Register register_6 (.D(or_2_out), .en(decoder_2_out5), .clk(CLK_out), .Q(register_6_q), .clr(CLR));
  Register register_7 (.D(or_2_out), .en(decoder_2_out6), .clk(CLK_out), .Q(register_7_q), .clr(CLR));
  Register register_8 (.D(or_2_out), .en(decoder_2_out7), .clk(CLK_out), .Q(register_8_q), .clr(CLR));
  Comparator comparator_1 (.a(rdata2), .b(register_1_q), .gt(comparator_1_gt), .lt(comparator_1_lt));  // open: eq
  and and_11 (and_11_out, multiplexer_3_out[3], decoder_1_out1);
  Multiplexer #(.select(3), .width(8)) multiplexer_5 (
    .in0(register_1_q), .in1(register_2_q), .in2(register_3_q), .in3(register_4_q), .in4(register_5_q),
    .in5(register_6_q), .in6(register_7_q), .in7(register_8_q), .out(rdata1), .sel(or_4_out));
  assign or_6_out = and_7_out | and_9_out;  // OR_Gate or_6, 3 bits wide
  Multiplexer #(.select(3), .width(8)) multiplexer_6 (
    .in0(register_1_q), .in1(register_2_q), .in2(register_3_q), .in3(register_4_q), .in4(register_5_q),
    .in5(register_6_q), .in6(register_7_q), .in7(register_8_q), .out(rdata2), .sel(or_6_out));
  Demultiplexer #(.select(3), .width(8)) demultiplexer_1 (
    .out0(demultiplexer_1_out0), .out1(demultiplexer_1_out1), .in(rdata1), .sel(multiplexer_3_out[2:0]));  // open: out2, out3, out4, out5, out6, out7
  Adder adder_2 (.a(rdata1), .b(rdata2), .out(adder_2_out));  // open: cin, cout
  Decoder #(.select(3)) decoder_3 (
    .out0(decoder_3_out0), .out1(decoder_3_out1), .sel(multiplexer_3_out[2:0]), .en(1'b1));  // open: out2, out3, out4, out5, out6, out7
  and and_12 (and_12_out, decoder_3_out0, and_11_out);
  and and_13 (and_13_out, decoder_3_out1, and_11_out);
  Register register_9 (.D(demultiplexer_1_out0), .en(and_12_out), .clk(CLK_out), .Q(register_9_q));  // open: clr
  Register register_10 (.D(demultiplexer_1_out1), .en(and_13_out), .clk(CLK_out), .Q(register_10_q));  // open: clr
  // LedBar #(.inputtype("row")) ledbar_1: pin names not known; wires that end beside it: register_9_q
  Hex_Digit_Display #(.decimalPoint("false")) hex_digit_display_1 (.value(register_10_q[7:4]));
  Hex_Digit_Display #(.decimalPoint("false")) hex_digit_display_2 (.value(register_10_q[3:0]));

  // Notes on the sheet:
  //   0
  //   rs2
  //   rs1
endmodule

module PC (
  input  [3:0] datain,
  input  ctr,
  input  CLK,
  input  CLR,
  output [3:0] PC_out
);

  wire [3:0] adder_1_out, multiplexer_1_out;

  Multiplexer #(.width(4)) multiplexer_1 (.in0(adder_1_out), .in1(datain), .out(multiplexer_1_out), .sel(ctr));
  Register #(.width(4)) register_1 (.D(multiplexer_1_out), .en(1'b1), .clk(CLK), .Q(PC_out), .clr(CLR));
  Adder #(.width(4)) adder_1 (.a(PC_out), .b(4'b0001), .out(adder_1_out));  // open: cin, cout
endmodule
